// Logisim project cpu_benchmark.circ as structural Verilog: 11 circuits, main circuit cpu
module cpu (
);

  wire beq, blez, bnq, Branch_t, clk, comparator_1_eq, condi_suc, half_word_t, halt, halt_g, not_1_out,
       PC_MUX_2, PC_MUX_3, RAM_LOAD, RAM_STO, registerfile_1_p3, RST, syscall_t, un_Branch_t, wb_1_we_out;
  wire [1:0] rA_t, rW_t, word_t, Y_t;
  wire [2:0] adder_2_out, register_1_q;
  wire [3:0] ALU_S;
  wire [4:0] multiplexer_2_out, registerfile_1_p4, registerfile_1_p5, registerfile_1_p6;
  wire [7:0] PC_q_2;
  wire [9:0] ex_mem_1_ctrl_msg_out;
  wire [11:0] adder_1_out, id_ex_1_pc_4_out, if_id_1_pc_4_out, multiplexer_1_out, npc_1_out_7, PC_4, PC_q;
  wire [13:0] controller_1_y;
  wire [13:2] id_ex_1_ctrl_msg_out;
  wire [15:0] \总周期数 , \无条件分支指令数 , \有条件分支成功跳转 , \有条件分支指令数 ;
  wire [31:0] A, alu_1_p4, B, bit_extender_1_out, ex_mem_1_alu_out, ex_mem_1_b_out, ex_mem_1_instruction_out,
       id_ex_1_a_out, id_ex_1_b_out, id_ex_1_instruction_out, if_id_1_instruction_out, mips_ram_1_p8,
       multiplexer_3_out, registerfile_1_p1, rom_1_data, SyscallOut, word_ctrl_1_out_4, y_ctrl_1_out_4;

  Button \u_总复位  (.out(RST));
  Register #(.width(12)) PC (
    .D(multiplexer_1_out), .en(halt), .Q({PC_q[11:10], PC_q_2, PC_q[1:0]}), .clk(clk), .clr(RST));
  Hex_Digit_Display hex_digit_display_1 (.value(SyscallOut[31:28]));  // open: dp
  Hex_Digit_Display hex_digit_display_2 (.value(SyscallOut[27:24]));  // open: dp
  Clock clock_1 (.out(clk));
  Hex_Digit_Display hex_digit_display_3 (.value(SyscallOut[23:20]));  // open: dp
  Hex_Digit_Display hex_digit_display_4 (.value(SyscallOut[19:16]));  // open: dp
  Adder #(.width(12)) adder_1 (
    .a({PC_q[11:10], PC_q_2, PC_q[1:0]}), .b(12'h4), .out(adder_1_out), .cin(1'b0));  // open: cout
  ROM #(.dataWidth(32)) rom_1 (.addr(PC_q_2), .data(rom_1_data));  // open: sel
  Hex_Digit_Display hex_digit_display_5 (.value(SyscallOut[15:12]));  // open: dp
  Hex_Digit_Display hex_digit_display_6 (.value(SyscallOut[11:8]));  // open: dp
  Hex_Digit_Display hex_digit_display_7 (.value(SyscallOut[3:0]));  // open: dp
  Hex_Digit_Display hex_digit_display_8 (.value(SyscallOut[7:4]));  // open: dp
  Multiplexer #(.width(12), .enable("false")) multiplexer_1 (
    .in0(npc_1_out_7), .in1(adder_1_out), .out(multiplexer_1_out), .sel(1'b1));
  IF_ID if_id_1 (
    .pc_4(adder_1_out), .CLK(clk), .pc_4_out(if_id_1_pc_4_out), .\同步清零 (1'b0), .\通行 (halt),
    .instruction(rom_1_data), .instruction_out(if_id_1_instruction_out));
  // Probe on \总周期数 
  // Probe on \无条件分支指令数 
  // Probe on \有条件分支指令数 
  // Probe on \有条件分支成功跳转 
  controller controller_1 (
    .in_1(if_id_1_instruction_out), .Branch(Branch_t), .rw(controller_1_y[13:12]), .Y(controller_1_y[1:0]),
    .Half_word(controller_1_y[2]), .un_Branch(un_Branch_t), .RAM_STO(controller_1_y[3]), .Ra(rA_t),
    .ALU_S(controller_1_y[7:4]), .syscall(syscall_t), .PC_MUX_2(PC_MUX_2), .blez(blez),
    .WE(controller_1_y[9]), .RAM_LOAD(RAM_LOAD), .PC_MUX_3(PC_MUX_3), .bnq(bnq), .w(controller_1_y[11:10]),
    .beq(beq));  // open: ALU_output
  condi_jump condi_jump_1 (.in_1(A), .out_6(condi_suc), .in_4(B), .in_2(blez), .in_3(beq), .in_5(bnq));
  // Probe on if_id_1_instruction_out
  npc npc_1 (
    .in_1(if_id_1_instruction_out), .in_2(if_id_1_pc_4_out), .out_7(npc_1_out_7), .in_3(condi_suc),
    .in_4(PC_MUX_2), .in_5(PC_MUX_3), .in_6(A));
  statistic statistic_1 (
    .out_10(\总周期数 ), .A(A), .out_11(\无条件分支指令数 ), .out_12(\有条件分支指令数 ), .B(B), .out_13(\有条件分支成功跳转 ),
    .in_6(clk), .in_7(RST), .in_8(syscall_t), .out_14(SyscallOut), .in_9(condi_suc), .in_1(Branch_t),
    .in_3(un_Branch_t), .out_15(halt_g), .in_5(halt));
  // Probe on {controller_1_y[13:9], halt_g, controller_1_y[7:0]}
  // RegisterFile registerfile_1: pin names not known; wires that end beside it: registerfile_1_p1, clk, registerfile_1_p3, registerfile_1_p4, registerfile_1_p5, registerfile_1_p6, A, B
  // Probe on registerfile_1_p6
  read_reg_ctrl read_reg_ctrl_1 (
    .in_1(if_id_1_instruction_out), .in_2(rA_t), .out_3(registerfile_1_p5), .out_4(registerfile_1_p6));
  // Probe on registerfile_1_p4
  // Probe on A
  // Probe on B
  // Probe on registerfile_1_p5
  // Probe on registerfile_1_p1
  ID_EX id_ex_1 (
    .pc_4(if_id_1_pc_4_out), .pc_4_out(id_ex_1_pc_4_out), .instruction(if_id_1_instruction_out),
    .instruction_out(id_ex_1_instruction_out), .CLK(clk), .\同步清零 (1'b0), .\通行 (halt),
    .ctrl_msg({controller_1_y[13:9], halt_g, controller_1_y[7:0]}),
    .ctrl_msg_out({id_ex_1_ctrl_msg_out[13:8], ALU_S, id_ex_1_ctrl_msg_out[3:2], Y_t}), .A(A),
    .A_out(id_ex_1_a_out), .B(B), .B_out(id_ex_1_b_out));
  // Probe on id_ex_1_instruction_out
  // Probe on {id_ex_1_ctrl_msg_out[13:8], ALU_S, id_ex_1_ctrl_msg_out[3:2], Y_t}
  Y_ctrl y_ctrl_1 (.in_1(id_ex_1_instruction_out), .out_4(y_ctrl_1_out_4), .in_2(id_ex_1_b_out), .in_3(Y_t));
  // ALU alu_1: pin names not known; wires that end beside it: id_ex_1_a_out, y_ctrl_1_out_4, ALU_S, alu_1_p4, alu_1_p4, id_ex_1_b_out
  EX_MEM ex_mem_1 (
    .pc_4(id_ex_1_pc_4_out), .pc_4_out(PC_4), .instruction(id_ex_1_instruction_out),
    .instruction_out(ex_mem_1_instruction_out),
    .ctrl_msg({id_ex_1_ctrl_msg_out[13:8], ALU_S, id_ex_1_ctrl_msg_out[3:2], Y_t}),
    .ctrl_msg_out({rW_t, word_t, ex_mem_1_ctrl_msg_out[9:4], RAM_STO, half_word_t, ex_mem_1_ctrl_msg_out[1:0]}),
    .alu(alu_1_p4), .alu_out(ex_mem_1_alu_out), .CLK(clk), .\同步清零 (1'b0), .\通行 (halt), .B(id_ex_1_b_out),
    .B_out(ex_mem_1_b_out));
  // Probe on ex_mem_1_instruction_out
  // Probe on {rW_t, word_t, ex_mem_1_ctrl_msg_out[9:4], RAM_STO, half_word_t, ex_mem_1_ctrl_msg_out[1:0]}
  // MIPS_RAM mips_ram_1: pin names not known; wires that end beside it: ex_mem_1_alu_out[21:2], ex_mem_1_b_out, RAM_STO, 4'b1111, clk, RAM_LOAD, RST, mips_ram_1_p8, ex_mem_1_instruction_out[25:21]
  Multiplexer #(.select(2), .width(5), .enable("false")) multiplexer_2 (
    .in0(ex_mem_1_instruction_out[15:11]), .in1({5{1'b1}}), .in3(ex_mem_1_instruction_out[20:16]),
    .out(multiplexer_2_out), .sel(rW_t));  // open: in2
  assign bit_extender_1_out = {{20{1'b0}}, PC_4};  // Bit_Extender bit_extender_1
  word_ctrl word_ctrl_1 (
    .out_4(word_ctrl_1_out_4), .in_1(ex_mem_1_alu_out[1]), .in_2(half_word_t), .in_3(mips_ram_1_p8));
  Multiplexer #(.select(2), .width(32), .enable("false")) multiplexer_3 (
    .in0(ex_mem_1_alu_out), .in1(bit_extender_1_out), .in3(word_ctrl_1_out_4), .out(multiplexer_3_out),
    .sel(word_t));  // open: in2
  WB wb_1 (
    .halt(ex_mem_1_ctrl_msg_out[9]), .RW(multiplexer_2_out), .w(multiplexer_3_out), .CLK(clk),
    .halt_out(registerfile_1_p3), .rw_out(registerfile_1_p4), .w_out(registerfile_1_p1), .\同步清零 (1'b0),
    .\通行 (halt), .WE(ex_mem_1_ctrl_msg_out[8]), .WE_out(wb_1_we_out));
  Register #(.width(3)) register_1 (.D(adder_2_out), .en(not_1_out), .Q(register_1_q), .clk(clk));  // open: clr
  not not_1 (not_1_out, comparator_1_eq);
  Adder #(.width(3)) adder_2 (.a(register_1_q), .b(3'b001), .out(adder_2_out));  // open: cin, cout
  Comparator #(.width(3), .mode("unsigned")) comparator_1 (
    .a(adder_2_out), .b(3'b100), .eq(comparator_1_eq));  // open: gt, lt
  Multiplexer #(.enable("false")) multiplexer_4 (.in0(1'b1), .in1(wb_1_we_out), .out(halt), .sel(comparator_1_eq));

  // Notes on the sheet:
  //   数码管输出应该用寄存器锁存，否则显示数据只能一闪而过
  //   可以通过项目增加Logisim库的方式将前几次实验完成的电路作为子电路引入到本电路中使用
  //   contents of rom_1 (hex, n*v repeats v):
  //   20100000 20110000 20120000 20130000 36100000 36310001 36520002 36730003 ae100000 ae110004 ae120008
  //   ae13000c 2002000a 20110000 20120000 20130000 c
  //   数码管输出
  //   总复位信号应将除ROM以外所有存储组件全部清零
endmodule

module condi_jump (
  input  [31:0] in_1,
  input  in_2,
  input  in_3,
  input  [31:0] in_4,
  input  in_5,
  output out_6
);

  wire and_1_out, and_2_out, and_3_out, comparator_1_eq, comparator_2_eq, comparator_2_lt, not_1_out,
       or_1_out;

  Comparator #(.width(32)) comparator_1 (.a(in_1), .b(in_4), .eq(comparator_1_eq));  // open: gt, lt
  Comparator #(.width(32)) comparator_2 (
    .a(in_1), .b({32{1'b0}}), .eq(comparator_2_eq), .lt(comparator_2_lt));  // open: gt
  or or_1 (or_1_out, comparator_2_eq, comparator_2_lt);
  not not_1 (not_1_out, comparator_1_eq);
  and and_1 (and_1_out, in_2, or_1_out);
  and and_2 (and_2_out, in_3, comparator_1_eq);
  and and_3 (and_3_out, in_5, not_1_out);
  or or_2 (out_6, and_1_out, and_2_out, and_3_out);

  // Other names for the same wires on the sheet: A[31:0] = in_1; B[31:0] = in_4; beq = in_3; blez = in_2; bnq = in_5;
  //   condi_suc = out_6
endmodule

module npc (
  input  [31:0] in_1,
  input  [11:0] in_2,
  input  in_3,
  input  in_4,
  input  in_5,
  input  [31:0] in_6,
  output [11:0] out_7
);

  wire [27:0] bit_extender_2_out, shifter_1_out;
  wire [31:0] adder_1_out, bit_extender_1_out, bit_extender_3_out, multiplexer_1_out, multiplexer_2_out,
       shifter_2_out;
  wire [31:12] multiplexer_3_out;

  assign bit_extender_1_out = {{20{1'b0}}, in_2};  // Bit_Extender bit_extender_1
  assign bit_extender_2_out = {{2{1'b0}}, in_1[25:0]};  // Bit_Extender bit_extender_2
  assign bit_extender_3_out = {{16{in_1[15]}}, in_1[15:0]};  // Bit_Extender bit_extender_3
  Shifter #(.width(28)) shifter_1 (.in(bit_extender_2_out), .\dist (5'b00010), .out(shifter_1_out));
  Shifter #(.width(32)) shifter_2 (.in(bit_extender_3_out), .\dist (5'b00010), .out(shifter_2_out));
  Adder #(.width(32)) adder_1 (.a(bit_extender_1_out), .b(shifter_2_out), .out(adder_1_out), .cin(1'b0));  // open: cout
  Multiplexer #(.width(32), .enable("false")) multiplexer_1 (
    .in0(bit_extender_1_out), .in1(adder_1_out), .out(multiplexer_1_out), .sel(in_3));
  Multiplexer #(.width(32), .enable("false")) multiplexer_2 (
    .in0({bit_extender_1_out[3:0], shifter_1_out}), .in1(multiplexer_1_out), .out(multiplexer_2_out),
    .sel(in_4));
  Multiplexer #(.width(32), .enable("false")) multiplexer_3 (
    .in0(multiplexer_2_out), .in1(in_6), .out({multiplexer_3_out, out_7}), .sel(in_5));

  // Other names for the same wires on the sheet: npc[11:0] = out_7; A[31:0] = in_6; condi_suc = in_3;
  //   instruction[31:0] = in_1; pc_4[11:0] = in_2; PC_MUX_2 = in_4; PC_MUX_3 = in_5
endmodule

module statistic (
  input  in_1,
  input  [31:0] A,
  input  in_3,
  input  [31:0] B,
  input  in_5,
  input  in_6,
  input  in_7,
  input  in_8,
  input  in_9,
  output [15:0] out_10,
  output [15:0] out_11,
  output [15:0] out_12,
  output [15:0] out_13,
  output [31:0] out_14,
  output out_15
);

  wire and_1_out, and_2_out, comparator_1_eq, comparator_1_gt, comparator_1_lt, or_1_out;
  wire [15:0] incrementer_1_p2, \周期数目 ;

  Counter #(.width(16), .max('hffff)) counter_1 (
    .load(1'b0), .count(in_5), .Q(\周期数目 ), .clk(in_6), .clr(in_7));  // open: D, carry
  Counter #(.width(16), .max('hffff)) counter_2 (
    .load(1'b0), .count(in_1), .Q(out_11), .clk(in_6), .clr(in_7));  // open: D, carry
  Counter #(.width(16), .max('hffff)) counter_3 (
    .load(1'b0), .count(in_3), .Q(out_12), .clk(in_6), .clr(in_7));  // open: D, carry
  Counter #(.width(16), .max('hffff)) counter_4 (
    .load(1'b0), .count(in_9), .Q(out_13), .clk(in_6), .clr(in_7));  // open: D, carry
  Comparator #(.width(32)) comparator_1 (
    .a(A), .b(32'ha), .gt(comparator_1_gt), .eq(comparator_1_eq), .lt(comparator_1_lt));
  or or_1 (or_1_out, comparator_1_gt, comparator_1_lt);
  Register #(.width(32)) register_1 (.D(B), .en(and_1_out), .Q(out_14), .clk(in_6), .clr(in_7));
  and and_1 (and_1_out, or_1_out, in_8);
  not not_1 (out_15, and_2_out);
  and and_2 (and_2_out, comparator_1_eq, in_8);
  // Incrementer incrementer_1: pin names not known; wires that end beside it: \周期数目 , incrementer_1_p2
  Multiplexer #(.width(16), .enable("false")) multiplexer_1 (
    .in0(incrementer_1_p2), .in1(\周期数目 ), .out(out_10), .sel(in_5));

  // Other names for the same wires on the sheet: Branch_t = in_3; clk = in_6; condi_num[15:0] = out_12;
  //   condi_suc = in_9; condi_suc_num[15:0] = out_13; halt = out_15; rst = in_7; strong_halt = in_5; syscall_t = in_8;
  //   SyscallOut[31:0] = out_14; total_cycles[15:0] = out_10; un_Branch_t = in_1; uncondi_num[15:0] = out_11
endmodule

// Y_t
module Y_ctrl (
  input  [31:0] in_1,
  input  [31:0] in_2,
  input  [1:0] in_3,
  output [31:0] out_4
);

  wire [31:0] bit_extender_1_out, bit_extender_2_out;

  assign bit_extender_1_out = {{16{in_1[15]}}, in_1[15:0]};  // Bit_Extender bit_extender_1
  assign bit_extender_2_out = {{27{1'b0}}, in_1[10:6]};  // Bit_Extender bit_extender_2
  Multiplexer #(.select(2), .width(32), .enable("false")) multiplexer_1 (
    .in0(in_2), .in1(bit_extender_2_out), .in3(bit_extender_1_out), .out(out_4), .sel(in_3));  // open: in2

  // Other names for the same wires on the sheet: B[31:0] = in_2; instruction[31:0] = in_1; Y[31:0] = out_4;
  //   Y_t[1:0] = in_3
endmodule

module word_ctrl (
  input  in_1,
  input  in_2,
  input  [31:0] in_3,
  output [31:0] out_4
);

  wire [15:0] multiplexer_1_out;
  wire [31:0] bit_extender_1_out;

  Multiplexer #(.width(16), .enable("false")) multiplexer_1 (
    .in0(in_3[15:0]), .in1(in_3[31:16]), .out(multiplexer_1_out), .sel(in_1));
  Multiplexer #(.width(32), .enable("false")) multiplexer_2 (
    .in0(in_3), .in1(bit_extender_1_out), .out(out_4), .sel(in_2));
  assign bit_extender_1_out = {{16{multiplexer_1_out[15]}}, multiplexer_1_out};  // Bit_Extender bit_extender_1

  // Other names for the same wires on the sheet: D[31:0] = in_3; D_out[31:0] = out_4; half_word_t = in_2; wc = in_1
endmodule

module read_reg_ctrl (
  input  [31:0] in_1,
  input  [1:0] in_2,
  output [4:0] out_3,
  output [4:0] out_4
);

  Multiplexer #(.select(2), .width(5), .enable("false")) multiplexer_1 (
    .in0(in_1[25:21]), .in1(5'b00010), .in3(in_1[20:16]), .out(out_3), .sel(in_2));  // open: in2
  Multiplexer #(.select(2), .width(5), .enable("false")) multiplexer_2 (
    .in0(in_1[20:16]), .in1(5'b00100), .in3(in_1[25:21]), .out(out_4), .sel(in_2));  // open: in2

  // Other names for the same wires on the sheet: instruction[31:0] = in_1; rA[4:0] = out_3; rA_t[1:0] = in_2;
  //   rB[4:0] = out_4

  // Notes on the sheet:
  //   输入
  //   输出
endmodule

module IF_ID (
  input  [11:0] pc_4,
  input  [31:0] instruction,
  input  CLK,
  input  \同步清零 ,
  input  \通行 ,
  output [11:0] pc_4_out,
  output [31:0] instruction_out
);

  wire [11:0] multiplexer_1_out;
  wire [31:0] multiplexer_2_out;

  Multiplexer #(.width(12), .enable("false")) multiplexer_1 (
    .in0(pc_4), .in1({12{1'b0}}), .out(multiplexer_1_out), .sel(\同步清零 ));
  Multiplexer #(.width(32), .enable("false")) multiplexer_2 (
    .in0(instruction), .in1({32{1'b0}}), .out(multiplexer_2_out), .sel(\同步清零 ));
  Register #(.width(12)) register_1 (.D(multiplexer_1_out), .en(\通行 ), .Q(pc_4_out), .clk(CLK));  // open: clr
  Register #(.width(32)) register_2 (.D(multiplexer_2_out), .en(\通行 ), .Q(instruction_out), .clk(CLK));  // open: clr
endmodule

module ID_EX (
  input  [11:0] pc_4,
  input  [31:0] instruction,
  input  [13:0] ctrl_msg,
  input  [31:0] A,
  input  [31:0] B,
  input  CLK,
  input  \同步清零 ,
  input  \通行 ,
  output [11:0] pc_4_out,
  output [31:0] instruction_out,
  output [13:0] ctrl_msg_out,
  output [31:0] A_out,
  output [31:0] B_out
);

  wire [11:0] multiplexer_1_out;
  wire [13:0] multiplexer_3_out;
  wire [31:0] multiplexer_2_out, multiplexer_4_out, multiplexer_5_out;

  Multiplexer #(.width(12), .enable("false")) multiplexer_1 (
    .in0(pc_4), .in1({12{1'b0}}), .out(multiplexer_1_out), .sel(\同步清零 ));
  Multiplexer #(.width(32), .enable("false")) multiplexer_2 (
    .in0(instruction), .in1({32{1'b0}}), .out(multiplexer_2_out), .sel(\同步清零 ));
  Multiplexer #(.width(14), .enable("false")) multiplexer_3 (
    .in0(ctrl_msg), .in1({14{1'b0}}), .out(multiplexer_3_out), .sel(\同步清零 ));
  Multiplexer #(.width(32), .enable("false")) multiplexer_4 (
    .in0(A), .in1({32{1'b0}}), .out(multiplexer_4_out), .sel(\同步清零 ));
  Multiplexer #(.width(32), .enable("false")) multiplexer_5 (
    .in0(B), .in1({32{1'b0}}), .out(multiplexer_5_out), .sel(\同步清零 ));
  Register #(.width(12)) register_1 (.D(multiplexer_1_out), .en(\通行 ), .Q(pc_4_out), .clk(CLK));  // open: clr
  Register #(.width(32)) register_2 (.D(multiplexer_2_out), .en(\通行 ), .Q(instruction_out), .clk(CLK));  // open: clr
  Register #(.width(14)) register_3 (.D(multiplexer_3_out), .en(\通行 ), .Q(ctrl_msg_out), .clk(CLK));  // open: clr
  Register #(.width(32)) register_4 (.D(multiplexer_4_out), .en(\通行 ), .Q(A_out), .clk(CLK));  // open: clr
  Register #(.width(32)) register_5 (.D(multiplexer_5_out), .en(\通行 ), .Q(B_out), .clk(CLK));  // open: clr
endmodule

module EX_MEM (
  input  [11:0] pc_4,
  input  [31:0] instruction,
  input  [13:0] ctrl_msg,
  input  [31:0] alu,
  input  [31:0] B,
  input  CLK,
  input  \同步清零 ,
  input  \通行 ,
  output [11:0] pc_4_out,
  output [31:0] instruction_out,
  output [13:0] ctrl_msg_out,
  output [31:0] alu_out,
  output [31:0] B_out
);

  wire [11:0] multiplexer_1_out;
  wire [13:0] multiplexer_3_out;
  wire [31:0] multiplexer_2_out, multiplexer_4_out, multiplexer_5_out;

  Multiplexer #(.width(12), .enable("false")) multiplexer_1 (
    .in0(pc_4), .in1({12{1'b0}}), .out(multiplexer_1_out), .sel(\同步清零 ));
  Multiplexer #(.width(32), .enable("false")) multiplexer_2 (
    .in0(instruction), .in1({32{1'b0}}), .out(multiplexer_2_out), .sel(\同步清零 ));
  Multiplexer #(.width(14), .enable("false")) multiplexer_3 (
    .in0(ctrl_msg), .in1({14{1'b0}}), .out(multiplexer_3_out), .sel(\同步清零 ));
  Multiplexer #(.width(32), .enable("false")) multiplexer_4 (
    .in0(alu), .in1({32{1'b0}}), .out(multiplexer_4_out), .sel(\同步清零 ));
  Multiplexer #(.width(32), .enable("false")) multiplexer_5 (
    .in0(B), .in1({32{1'b0}}), .out(multiplexer_5_out), .sel(\同步清零 ));
  Register #(.width(12)) register_1 (.D(multiplexer_1_out), .en(\通行 ), .Q(pc_4_out), .clk(CLK));  // open: clr
  Register #(.width(32)) register_2 (.D(multiplexer_2_out), .en(\通行 ), .Q(instruction_out), .clk(CLK));  // open: clr
  Register #(.width(14)) register_3 (.D(multiplexer_3_out), .en(\通行 ), .Q(ctrl_msg_out), .clk(CLK));  // open: clr
  Register #(.width(32)) register_4 (.D(multiplexer_4_out), .en(\通行 ), .Q(alu_out), .clk(CLK));  // open: clr
  Register #(.width(32)) register_5 (.D(multiplexer_5_out), .en(\通行 ), .Q(B_out), .clk(CLK));  // open: clr
endmodule

module WB (
  input  halt,
  input  WE,
  input  [4:0] RW,
  input  [31:0] w,
  input  CLK,
  input  \同步清零 ,
  input  \通行 ,
  output halt_out,
  output WE_out,
  output [4:0] rw_out,
  output [31:0] w_out
);

  wire multiplexer_1_out, multiplexer_2_out;
  wire [4:0] multiplexer_3_out;
  wire [31:0] multiplexer_4_out;

  Multiplexer #(.enable("false")) multiplexer_1 (.in0(halt), .in1(1'b0), .out(multiplexer_1_out), .sel(\同步清零 ));
  Multiplexer #(.enable("false")) multiplexer_2 (.in0(WE), .in1(1'b0), .out(multiplexer_2_out), .sel(\同步清零 ));
  Multiplexer #(.width(5), .enable("false")) multiplexer_3 (
    .in0(RW), .in1({5{1'b0}}), .out(multiplexer_3_out), .sel(\同步清零 ));
  Multiplexer #(.width(32), .enable("false")) multiplexer_4 (
    .in0(w), .in1({32{1'b0}}), .out(multiplexer_4_out), .sel(\同步清零 ));
  Register #(.width(1)) register_1 (.D(multiplexer_1_out), .en(\通行 ), .Q(halt_out), .clk(CLK));  // open: clr
  Register #(.width(1)) register_2 (.D(multiplexer_2_out), .en(\通行 ), .Q(WE_out), .clk(CLK));  // open: clr
  Register #(.width(5)) register_3 (.D(multiplexer_3_out), .en(\通行 ), .Q(rw_out), .clk(CLK));  // open: clr
  Register #(.width(32)) register_4 (.D(multiplexer_4_out), .en(\通行 ), .Q(w_out), .clk(CLK));  // open: clr
endmodule
