// Logisim project interupt.circ as structural Verilog: 14 circuits, main circuit cpu
module cpu (
);

  wire ALU_output, and_1_out, beq, blez, bnq, Branch_t, clk, comparator_1_eq, condi_suc, \continue ,
       counter_1_q, demultiplexer_1_out1, demultiplexer_1_out2, demultiplexer_1_out3, eret, half_word_t,
       halt, int_one, int_three, int_two, multiplexer_5_out, not_1_out, PC_MUX_2, PC_MUX_3, RAM_LOAD,
       RAM_STO, register_ctrl_1_out_5, RST, stop, syscall_t, un_Branch_t, W1, W2, W3, wc, WE_t;
  wire [0:0] IE_ctrl;
  wire [1:0] int_num, rA_t, register_1_q, rW_t, w_t, Y_t;
  wire [3:0] ALU_S;
  wire [4:0] register_ctrl_1_out_6, register_ctrl_1_out_7, register_ctrl_1_out_8;
  wire [11:0] multiplexer_1_out, multiplexer_2_out, multiplexer_3_out, npc_1_out_7, PC_q, pc_reg_1_r;
  wire [15:0] \总周期数 , \无条件分支指令数 , \有条件分支成功跳转 , \有条件分支指令数 ;
  wire [19:0] alu_1_p4_2;
  wire [31:0] A, alu_1_p4, B, bit_extender_1_out, instruction, mips_ram_1_p8, multiplexer_4_out, PC_4,
       SyscallOut, word_ctrl_1_out_4, y_ctrl_1_out_4;

  Button \u_总复位  (.out(RST));
  Button \u_中断１  (.out(int_one));
  Button \u_中断２  (.out(int_two));
  Button \u_中断３  (.out(int_three));
  Register #(.width(12)) PC (.D(multiplexer_1_out), .en(and_1_out), .Q(PC_q), .clk(clk), .clr(RST));
  Hex_Digit_Display hex_digit_display_1 (.value(SyscallOut[31:28]));  // open: dp
  Hex_Digit_Display hex_digit_display_2 (.value(SyscallOut[27:24]));  // open: dp
  Multiplexer #(.width(12), .enable("false")) multiplexer_1 (
    .in0(npc_1_out_7), .in1(pc_reg_1_r), .out(multiplexer_1_out), .sel(eret));
  Multiplexer #(.select(2), .width(12)) multiplexer_2 (
    .in1(12'h488), .in2(12'h52c), .in3(12'h5d0), .out(multiplexer_2_out), .sel(int_num));  // open: in0, en
  // Probe on multiplexer_2_out
  Clock clock_1 (.out(clk));
  Hex_Digit_Display hex_digit_display_3 (.value(SyscallOut[23:20]));  // open: dp
  Hex_Digit_Display hex_digit_display_4 (.value(SyscallOut[19:16]));  // open: dp
  assign bit_extender_1_out = {{20{1'b0}}, multiplexer_3_out};  // Bit_Extender bit_extender_1
  Multiplexer #(.width(12)) multiplexer_3 (
    .in0(PC_q), .in1(multiplexer_2_out), .out(multiplexer_3_out), .sel(IE_ctrl[0]));  // open: en
  Hex_Digit_Display hex_digit_display_5 (.value(SyscallOut[11:8]));  // open: dp
  Hex_Digit_Display hex_digit_display_6 (.value(SyscallOut[15:12]));  // open: dp
  pc_reg pc_reg_1 (.R(pc_reg_1_r), .W(PC_q), .clk(clk), .\int (IE_ctrl[0]), .eret(eret));
  ROM #(.addrWidth(10), .dataWidth(32)) rom_1 (.addr(multiplexer_3_out[11:2]), .data(instruction));  // open: sel
  Hex_Digit_Display hex_digit_display_7 (.value(SyscallOut[7:4]));  // open: dp
  Hex_Digit_Display hex_digit_display_8 (.value(SyscallOut[3:0]));  // open: dp
  Button u_continue (.out(\continue ));
  Adder #(.width(32)) adder_1 (.a(bit_extender_1_out), .b(32'h4), .out(PC_4), .cin(1'b0));  // open: cout
  Multiplexer #(.select(2), .width(32), .enable("false")) multiplexer_4 (
    .in0({alu_1_p4[31:22], alu_1_p4_2, wc, alu_1_p4[0]}), .in1(PC_4), .in3(word_ctrl_1_out_4),
    .out(multiplexer_4_out), .sel(w_t));  // open: in2
  controller controller_1 (
    .in_1(instruction), .Branch(Branch_t), .rw(rW_t), .Y(Y_t), .Half_word(half_word_t),
    .un_Branch(un_Branch_t), .RAM_STO(RAM_STO), .Ra(rA_t), .ALU_S(ALU_S), .syscall(syscall_t),
    .PC_MUX_2(PC_MUX_2), .blez(blez), .WE(WE_t), .RAM_LOAD(RAM_LOAD), .PC_MUX_3(PC_MUX_3), .bnq(bnq),
    .w(w_t), .beq(beq), .ALU_output(ALU_output));
  npc npc_1 (
    .in_1(instruction), .in_2(PC_4), .out_7(npc_1_out_7), .in_3(condi_suc), .in_4(PC_MUX_2), .in_5(PC_MUX_3),
    .in_6(A));
  condi_jump condi_jump_1 (.in_1(A), .out_6(condi_suc), .in_4(B), .in_2(blez), .in_3(beq), .in_5(bnq));
  register_ctrl register_ctrl_1 (
    .in_1(instruction), .in_3(rW_t), .in_2(rA_t), .in_4(WE_t), .out_5(register_ctrl_1_out_5),
    .out_6(register_ctrl_1_out_6), .out_7(register_ctrl_1_out_7), .out_8(register_ctrl_1_out_8));
  // Probe on \总周期数 
  // Probe on \无条件分支指令数 
  // Probe on \有条件分支指令数 
  // Probe on \有条件分支成功跳转 
  // RegisterFile registerfile_1: pin names not known; wires that end beside it: multiplexer_4_out, clk, register_ctrl_1_out_5, register_ctrl_1_out_6, register_ctrl_1_out_7, register_ctrl_1_out_8, A, B
  // Probe on B
  Y_ctrl y_ctrl_1 (.in_1(instruction), .out_4(y_ctrl_1_out_4), .in_2(B), .in_3(Y_t));
  // Probe on instruction
  Counter #(.width(1), .max('h1)) counter_1 (
    .count(stop), .Q(counter_1_q), .clk(clk), .clr(\continue ));  // open: load, D, carry
  Multiplexer #(.select(2), .enable("false")) multiplexer_5 (
    .in0(1'b1), .in1(1'b0), .in2(1'b1), .in3(1'b1), .out(multiplexer_5_out), .sel({eret, IE_ctrl[0]}));
  // Probe on A
  // Probe on y_ctrl_1_out_4
  not not_1 (not_1_out, counter_1_q);
  statistic statistic_1 (
    .out_10(\总周期数 ), .in_2(A), .out_11(\无条件分支指令数 ), .out_12(\有条件分支指令数 ), .in_4(B), .out_13(\有条件分支成功跳转 ),
    .in_6(clk), .in_7(RST), .in_8(syscall_t), .out_14(SyscallOut), .in_9(condi_suc), .in_1(Branch_t),
    .in_3(un_Branch_t), .out_15(halt), .in_5(counter_1_q));
  // Probe on IE_ctrl[0]
  LED led_1 (.in(W1));
  LED led_2 (.in(W2));
  LED led_3 (.in(W3));
  // Probe on int_num
  // ALU alu_1: pin names not known; wires that end beside it: A, y_ctrl_1_out_4, ALU_S, {alu_1_p4[31:22], alu_1_p4_2, wc, alu_1_p4[0]}
  // Probe on ALU_S
  and and_1 (and_1_out, halt, not_1_out);
  i_recognize i_recognize_1 (
    .interupt_one(int_one), .IE(multiplexer_5_out), .clear_one(demultiplexer_1_out1), .clk(clk),
    .interupt_two(int_two), .clear_two(demultiplexer_1_out2), .wait_one(W1), .start_interupt(IE_ctrl[0]),
    .wait_two(W2), .int_num(int_num), .interupt_three(int_three), .wait_three(W3),
    .clear_three(demultiplexer_1_out3));
  // Probe on {alu_1_p4[31:22], alu_1_p4_2, wc, alu_1_p4[0]}
  Comparator #(.width(32)) comparator_1 (.a(A), .b(32'h32), .eq(comparator_1_eq));  // open: gt, lt
  Comparator #(.width(32)) comparator_2 (.a(32'h42000018), .b(instruction), .eq(eret));  // open: gt, lt
  Demultiplexer #(.select(2), .enable("false")) demultiplexer_1 (
    .out1(demultiplexer_1_out1), .out2(demultiplexer_1_out2), .out3(demultiplexer_1_out3), .in(eret),
    .sel(register_1_q));  // open: out0
  Register #(.width(2)) register_1 (.D(int_num), .Q(register_1_q), .clk(clk));  // open: en, clr
  and and_2 (stop, comparator_1_eq, syscall_t);
  // MIPS_RAM mips_ram_1: pin names not known; wires that end beside it: alu_1_p4_2, B, RAM_STO, 4'b1111, clk, RAM_LOAD, RST, mips_ram_1_p8
  word_ctrl word_ctrl_1 (.out_4(word_ctrl_1_out_4), .in_1(wc), .in_2(half_word_t), .in_3(mips_ram_1_p8));

  // Other names for the same wires on the sheet: interrupt_start = IE_ctrl[0]; IE_ctrl[1] = eret

  // Notes on the sheet:
  //   contents of rom_1 (hex, n*v repeats v):
  //   201d0080 20020032 c 20110001 8000c08 20110001 20120002 20130003 8000c0c 20110001 20120002 20130003
  //   8000c10 20110001 20120002 20130003 8000c14 20110001 20120002 20130003 c000cff 20100001 20110001
  //   118fc0 112020 20020022 c 118882 12200001 8000c18 112020 20020022 c 20110001 118880 112020 20020022 c
  //   12200001 8000c22 20110001 118fc0 112020 20020022 c 1188c3 112020 20020022 c 118903 112020 20020022 c
  //   118903 112020 20020022 c 118903 112020 20020022 c 118903 112020 20020022 c 118903 112020 20020022 c
  //   118903 112020 20020022 c 118903 112020 20020022 c 20100001 109fc0 139fc3 8021 2012000c 24160003
  //   26100001 3210000f 20080008 20090001 139900 2709825 132020 20020022 c 1094022 1500fff9 22100001
  //   2018000f 2188024 108700 20080008 20090001 139902 2709825 132021 20020022 c 1094022 1500fff9 108702
  //   2c9b022 12c00001 8000c53 4020 1084027 84400 3508ffff 82021 20020022 c 2010ffff 20110000 ae300000
  //   22100001 22310004 ae300000 22100001 22310004 ae300000 22100001 22310004 ae300000 22100001 22310004
  //   ae300000 22100001 22310004 ae300000 22100001 22310004 ae300000 22100001 22310004 ae300000 22100001
  //   22310004 ae300000 22100001 22310004 ae300000 22100001 22310004 ae300000 22100001 22310004 ae300000
  //   22100001 22310004 ae300000 22100001 22310004 ae300000 22100001 22310004 ae300000 22100001 22310004
  //   ae300000 22100001 22310004 22100001 8020 2011003c 8e130000 8e340000 274402a 11000002 ae330000
  //   ae140000 2231fffc 1611fff8 102020 20020022 c 22100004 2011003c 1611fff2 20020032 c 20080001 20090003
  //   20110876 118d00 112020 20020022 c 200b0008 1118806 1318806 112020 20020022 c 216bffff 1560fff9
  //   20020032 c 20080001 20090003 20110876 118d00 112020 20020022 c 200b0008 1118807 1318807 112020
  //   20020022 c 216bffff 1560fff9 20020032 c 20090000 200b0010 34118483 20120404 118c00 129400 36318281
  //   22520404 ad310000 2328820 21290004 216bffff 1560fffb 200b0020 20090000 85310000 112020 20020022 c
  //   21290002 216bffff 1560fff9 20020032 c 2011fff1 112020 20020022 c 22310001 1a20fffb 20020032 c
  //   2002000a c 20100000 22100001 102020 20020022 c 22100002 102020 20020022 c 22100003 102020 20020022 c
  //   22100004 102020 20020022 c 22100005 102020 20020022 c 22100006 102020 20020022 c 22100007 102020
  //   20020022 c 22100008 102020 20020022 20020022 c 3e00008 27bdfffc afb00000 27bdfffc afb30000 27bdfffc
  //   afb40000 27bdfffc afb50000 27bdfffc afb60000 27bdfffc afa40000 27bdfffc afa20000 20160001 20140006
  //   20150001 168020 108100 2149825 132020 20020022 c 1600fffa 295a022 1680fff7 8fa20000 27bd0004
  //   8fa40000 27bd0004 8fb60000 27bd0004 8fb50000 27bd0004 8fb40000 27bd0004 8fb30000 27bd0004 8fb00000
  //   27bd0004 42000018 27bdfffc afb00000 27bdfffc afb30000 27bdfffc afb40000 27bdfffc afb50000 27bdfffc
  //   afb60000 27bdfffc afa40000 27bdfffc afa20000 20160002 20140006 20150001 168020 108100 2149825 132020
  //   20020022 c 1600fffa 295a022 1680fff7 8fa20000 27bd0004 8fa40000 27bd0004 8fb60000 27bd0004 8fb50000
  //   27bd0004 8fb40000 27bd0004 8fb30000 27bd0004 8fb00000 27bd0004 42000018 27bdfffc afb00000 27bdfffc
  //   afb30000 27bdfffc afb40000 27bdfffc afb50000 27bdfffc afb60000 27bdfffc afa40000 27bdfffc afa20000
  //   20160003 20140006 20150001 168020 108100 2149825 132020 20020022 c 1600fffa 295a022 1680fff7
  //   8fa20000 27bd0004 8fa40000 27bd0004 8fb60000 27bd0004 8fb50000 27bd0004 8fb40000 27bd0004 8fb30000
  //   27bd0004 8fb00000 27bd0004 42000018
  //   数码管输出
endmodule

module register_ctrl (
  input  [31:0] in_1,
  input  [1:0] in_2,
  input  [1:0] in_3,
  input  in_4,
  output out_5,
  output [4:0] out_6,
  output [4:0] out_7,
  output [4:0] out_8
);

  Multiplexer #(.select(2), .width(5), .enable("false")) multiplexer_1 (
    .in0(in_1[15:11]), .in1({5{1'b1}}), .in3(in_1[20:16]), .out(out_6), .sel(in_3));  // open: in2
  Multiplexer #(.select(2), .width(5), .enable("false")) multiplexer_2 (
    .in0(in_1[25:21]), .in1(5'b00010), .in3(in_1[20:16]), .out(out_7), .sel(in_2));  // open: in2
  Multiplexer #(.select(2), .width(5), .enable("false")) multiplexer_3 (
    .in0(in_1[20:16]), .in1(5'b00100), .in3(in_1[25:21]), .out(out_8), .sel(in_2));  // open: in2

  assign out_5 = in_4;

  // Other names for the same wires on the sheet: instruction[31:0] = in_1; rA[4:0] = out_7; rA_t[1:0] = in_2;
  //   rB[4:0] = out_8; rW[4:0] = out_6; rW_t[1:0] = in_3; WE = in_4; WE_t = in_4

  // Notes on the sheet:
  //   输入
  //   输出
endmodule

module condi_jump (
  input  [31:0] in_1,
  input  in_2,
  input  in_3,
  input  [31:0] in_4,
  input  in_5,
  output out_6
);

  wire and_1_out, and_2_out, and_3_out, comparator_1_eq, comparator_2_eq, comparator_2_lt, not_1_out,
       or_1_out;

  Comparator #(.width(32)) comparator_1 (.a(in_1), .b(in_4), .eq(comparator_1_eq));  // open: gt, lt
  Comparator #(.width(32)) comparator_2 (
    .a(in_1), .b({32{1'b0}}), .eq(comparator_2_eq), .lt(comparator_2_lt));  // open: gt
  or or_1 (or_1_out, comparator_2_eq, comparator_2_lt);
  not not_1 (not_1_out, comparator_1_eq);
  and and_1 (and_1_out, in_2, or_1_out);
  and and_2 (and_2_out, in_3, comparator_1_eq);
  and and_3 (and_3_out, in_5, not_1_out);
  or or_2 (out_6, and_1_out, and_2_out, and_3_out);

  // Other names for the same wires on the sheet: A[31:0] = in_1; B[31:0] = in_4; beq = in_3; blez = in_2; bnq = in_5;
  //   condi_suc = out_6
endmodule

module npc (
  input  [31:0] in_1,
  input  [31:0] in_2,
  input  in_3,
  input  in_4,
  input  in_5,
  input  [31:0] in_6,
  output [11:0] out_7
);

  wire [27:0] bit_extender_1_out, shifter_1_out;
  wire [31:0] adder_1_out, bit_extender_2_out, multiplexer_1_out, multiplexer_2_out, shifter_2_out;
  wire [31:12] multiplexer_3_out;

  assign bit_extender_1_out = {{2{1'b0}}, in_1[25:0]};  // Bit_Extender bit_extender_1
  assign bit_extender_2_out = {{16{in_1[15]}}, in_1[15:0]};  // Bit_Extender bit_extender_2
  Shifter #(.width(28)) shifter_1 (.in(bit_extender_1_out), .\dist (5'b00010), .out(shifter_1_out));
  Shifter #(.width(32)) shifter_2 (.in(bit_extender_2_out), .\dist (5'b00010), .out(shifter_2_out));
  Adder #(.width(32)) adder_1 (.a(in_2), .b(shifter_2_out), .out(adder_1_out), .cin(1'b0));  // open: cout
  Multiplexer #(.width(32), .enable("false")) multiplexer_1 (
    .in0(in_2), .in1(adder_1_out), .out(multiplexer_1_out), .sel(in_3));
  Multiplexer #(.width(32), .enable("false")) multiplexer_2 (
    .in0({in_2[3:0], shifter_1_out}), .in1(multiplexer_1_out), .out(multiplexer_2_out), .sel(in_4));
  Multiplexer #(.width(32), .enable("false")) multiplexer_3 (
    .in0(multiplexer_2_out), .in1(in_6), .out({multiplexer_3_out, out_7}), .sel(in_5));

  // Other names for the same wires on the sheet: pc_4[31:0] = in_2; npc[11:0] = out_7; A[31:0] = in_6;
  //   condi_suc = in_3; instruction[31:0] = in_1; PC_MUX_2 = in_4; PC_MUX_3 = in_5
endmodule

module statistic (
  input  in_1,
  input  [31:0] in_2,
  input  in_3,
  input  [31:0] in_4,
  input  in_5,
  input  in_6,
  input  in_7,
  input  in_8,
  input  in_9,
  output [15:0] out_10,
  output [15:0] out_11,
  output [15:0] out_12,
  output [15:0] out_13,
  output [31:0] out_14,
  output out_15
);

  wire and_1_out, and_2_out, and_3_out, and_4_out, comparator_1_eq, comparator_2_eq, comparator_3_eq,
       not_1_out, stop;
  wire [15:0] incrementer_1_p2, \周期数目 ;

  and and_1 (and_1_out, out_15, not_1_out);
  not not_1 (not_1_out, in_5);
  Counter #(.width(16), .max('hffff)) counter_1 (
    .load(1'b0), .count(and_1_out), .Q(\周期数目 ), .clk(in_6), .clr(in_7));  // open: D, carry
  Counter #(.width(16), .max('hffff)) counter_2 (
    .load(1'b0), .count(in_1), .Q(out_11), .clk(in_6), .clr(in_7));  // open: D, carry
  Counter #(.width(16), .max('hffff)) counter_3 (
    .load(1'b0), .count(in_3), .Q(out_12), .clk(in_6), .clr(in_7));  // open: D, carry
  Comparator #(.width(32)) comparator_1 (.a(in_2), .b(32'h32), .eq(comparator_1_eq));  // open: gt, lt
  Counter #(.width(16), .max('hffff)) counter_4 (
    .load(1'b0), .count(in_9), .Q(out_13), .clk(in_6), .clr(in_7));  // open: D, carry
  and and_2 (and_2_out, comparator_1_eq, in_8);
  not not_2 (stop, and_2_out);
  Comparator #(.width(32)) comparator_2 (.a(in_2), .b(32'h22), .eq(comparator_2_eq));  // open: gt, lt
  Comparator #(.width(32)) comparator_3 (.a(in_2), .b(32'ha), .eq(comparator_3_eq));  // open: gt, lt
  Register #(.width(32)) register_1 (.D(in_4), .en(and_3_out), .Q(out_14), .clk(in_6), .clr(in_7));
  and and_3 (and_3_out, comparator_2_eq, in_8);
  and and_4 (and_4_out, comparator_3_eq, in_8);
  // Incrementer incrementer_1: pin names not known; wires that end beside it: \周期数目 , incrementer_1_p2
  not not_3 (out_15, and_4_out);
  Multiplexer #(.width(16), .enable("false")) multiplexer_1 (
    .in0(incrementer_1_p2), .in1(\周期数目 ), .out(out_10), .sel(out_15));

  // Other names for the same wires on the sheet: A[31:0] = in_2; B[31:0] = in_4; Branch_t = in_3; clk = in_6;
  //   condi_num[15:0] = out_12; condi_suc = in_9; condi_suc_num[15:0] = out_13; halt = out_15; out_stop = in_5;
  //   rst = in_7; syscall_t = in_8; SyscallOut[31:0] = out_14; total_cycles[15:0] = out_10; un_Branch_t = in_1;
  //   uncondi_num[15:0] = out_11
endmodule

// Y_t
module Y_ctrl (
  input  [31:0] in_1,
  input  [31:0] in_2,
  input  [1:0] in_3,
  output [31:0] out_4
);

  wire ori_andi;
  wire [31:0] bit_extender_1_out, bit_extender_2_out, bit_extender_3_out, multiplexer_1_out;

  // Probe on in_1[31:27]
  Comparator #(.width(5), .mode("unsigned")) comparator_1 (
    .a(in_1[31:27]), .b(5'b00110), .eq(ori_andi));  // open: gt, lt
  // Probe on in_1
  assign bit_extender_1_out = {{16{in_1[15]}}, in_1[15:0]};  // Bit_Extender bit_extender_1
  assign bit_extender_2_out = {{16{1'b0}}, in_1[15:0]};  // Bit_Extender bit_extender_2
  Multiplexer #(.width(32), .enable("false")) multiplexer_1 (
    .in0(bit_extender_1_out), .in1(bit_extender_2_out), .out(multiplexer_1_out), .sel(ori_andi));
  assign bit_extender_3_out = {{27{1'b0}}, in_1[10:6]};  // Bit_Extender bit_extender_3
  Multiplexer #(.select(2), .width(32), .enable("false")) multiplexer_2 (
    .in0(in_2), .in1(bit_extender_3_out), .in3(multiplexer_1_out), .out(out_4), .sel(in_3));  // open: in2

  // Other names for the same wires on the sheet: B[31:0] = in_2; instruction[31:0] = in_1; Y[31:0] = out_4;
  //   Y_t[1:0] = in_3
endmodule

module word_ctrl (
  input  in_1,
  input  in_2,
  input  [31:0] in_3,
  output [31:0] out_4
);

  wire [15:0] multiplexer_1_out;
  wire [31:0] bit_extender_1_out;

  Multiplexer #(.width(16), .enable("false")) multiplexer_1 (
    .in0(in_3[15:0]), .in1(in_3[31:16]), .out(multiplexer_1_out), .sel(in_1));
  Multiplexer #(.width(32), .enable("false")) multiplexer_2 (
    .in0(in_3), .in1(bit_extender_1_out), .out(out_4), .sel(in_2));
  assign bit_extender_1_out = {{16{multiplexer_1_out[15]}}, multiplexer_1_out};  // Bit_Extender bit_extender_1

  // Other names for the same wires on the sheet: D[31:0] = in_3; D_out[31:0] = out_4; half_word_t = in_2; wc = in_1
endmodule

module IF_ID (
  input  [15:0] Din16,
  input  \传输状态In ,
  input  CLK,
  input  \同步清零 ,
  output [15:0] Dout16,
  output \传输状态Out 
);

  wire multiplexer_2_out;
  wire [15:0] multiplexer_1_out;

  Multiplexer #(.width(16), .enable("false")) multiplexer_1 (
    .in0(Din16), .in1({16{1'b0}}), .out(multiplexer_1_out), .sel(\同步清零 ));
  Multiplexer #(.enable("false")) multiplexer_2 (.in0(\传输状态In ), .in1(1'b0), .out(multiplexer_2_out), .sel(\同步清零 ));
  Register #(.width(16)) register_1 (.D(multiplexer_1_out), .en(\传输状态In ), .Q(Dout16), .clk(CLK));  // open: clr
  Register #(.width(1)) register_2 (.D(multiplexer_2_out), .en(\传输状态In ), .Q(\传输状态Out ), .clk(CLK));  // open: clr
endmodule

module ID_EX (
  input  [15:0] Din16,
  input  \传输状态In ,
  input  CLK,
  input  \同步清零 ,
  output [15:0] Dout16,
  output \传输状态Out 
);

  wire multiplexer_2_out;
  wire [15:0] multiplexer_1_out;

  Multiplexer #(.width(16), .enable("false")) multiplexer_1 (
    .in0(Din16), .in1({16{1'b0}}), .out(multiplexer_1_out), .sel(\同步清零 ));
  Multiplexer #(.enable("false")) multiplexer_2 (.in0(\传输状态In ), .in1(1'b0), .out(multiplexer_2_out), .sel(\同步清零 ));
  Register #(.width(16)) register_1 (.D(multiplexer_1_out), .en(\传输状态In ), .Q(Dout16), .clk(CLK));  // open: clr
  Register #(.width(1)) register_2 (.D(multiplexer_2_out), .en(\传输状态In ), .Q(\传输状态Out ), .clk(CLK));  // open: clr
endmodule

module EX_MEM (
  input  [15:0] Din16,
  input  \传输状态In ,
  input  CLK,
  input  \同步清零 ,
  output [15:0] Dout16,
  output \传输状态Out 
);

  wire multiplexer_2_out;
  wire [15:0] multiplexer_1_out;

  Multiplexer #(.width(16), .enable("false")) multiplexer_1 (
    .in0(Din16), .in1({16{1'b0}}), .out(multiplexer_1_out), .sel(\同步清零 ));
  Multiplexer #(.enable("false")) multiplexer_2 (.in0(\传输状态In ), .in1(1'b0), .out(multiplexer_2_out), .sel(\同步清零 ));
  Register #(.width(16)) register_1 (.D(multiplexer_1_out), .en(\传输状态In ), .Q(Dout16), .clk(CLK));  // open: clr
  Register #(.width(1)) register_2 (.D(multiplexer_2_out), .en(\传输状态In ), .Q(\传输状态Out ), .clk(CLK));  // open: clr
endmodule

module WB (
  input  [15:0] Din16,
  input  \传输状态In ,
  input  CLK,
  input  \同步清零 ,
  output [15:0] Dout16,
  output \传输状态Out 
);

  wire multiplexer_2_out;
  wire [15:0] multiplexer_1_out;

  Multiplexer #(.width(16), .enable("false")) multiplexer_1 (
    .in0(Din16), .in1({16{1'b0}}), .out(multiplexer_1_out), .sel(\同步清零 ));
  Multiplexer #(.enable("false")) multiplexer_2 (.in0(\传输状态In ), .in1(1'b0), .out(multiplexer_2_out), .sel(\同步清零 ));
  Register #(.width(16)) register_1 (.D(multiplexer_1_out), .en(\传输状态In ), .Q(Dout16), .clk(CLK));  // open: clr
  Register #(.width(1)) register_2 (.D(multiplexer_2_out), .en(\传输状态In ), .Q(\传输状态Out ), .clk(CLK));  // open: clr
endmodule

module ig (
  input  clk,
  input  \同步清零 ,
  input  interupt,
  output \wait ,
  output interupt_request
);

  wire and_1_out, d_ff_1_q, or_2_out;

  or or_1 (\wait , interupt_request, d_ff_1_q);
  D_Flip_Flop d_ff_1 (.clk(interupt), .D(1'b1), .Q(d_ff_1_q), .reset(interupt_request));  // open: Qn, preset, en
  or or_2 (or_2_out, d_ff_1_q, interupt_request);
  and and_1 (and_1_out, or_2_out, ~\同步清零 );  // AND_Gate
  D_Flip_Flop d_ff_2 (.clk(clk), .D(and_1_out), .Q(interupt_request));  // open: Qn, preset, en, reset

  // Other names for the same wires on the sheet: clear = \同步清零 ; wait_sig = \wait 
endmodule

// INT
module i_recognize (
  input  interupt_one,
  input  IE,
  input  clear_one,
  input  clk,
  input  interupt_two,
  input  clear_two,
  input  interupt_three,
  input  clear_three,
  output wait_one,
  output start_interupt,
  output wait_two,
  output [1:0] int_num,
  output wait_three
);

  wire and_1_out, and_2_out, and_3_out, and_5_out, comparator_1_gt, comparator_1_lt, d_ff_1_q, d_ff_2_q,
       d_ff_3_q, demultiplexer_1_out1, demultiplexer_1_out2, demultiplexer_1_out3, multiplexer_1_out,
       not_1_out, not_2_out, one_exe, one_interupt_request, or_1_out, three_exe, two_2_interupt_request,
       two_exe, two_interupt_request;
  wire [1:0] register_1_q;

  ig one (
    .\wait (wait_one), .clk(clk), .interupt_request(one_interupt_request), .\同步清零 (clear_one),
    .interupt(interupt_one));
  ig two (
    .\wait (wait_two), .clk(clk), .interupt_request(two_interupt_request), .\同步清零 (clear_two),
    .interupt(interupt_two));
  ig two_2 (
    .\wait (wait_three), .clk(clk), .interupt_request(two_2_interupt_request), .\同步清零 (clear_three),
    .interupt(interupt_three));
  D_Flip_Flop d_ff_1 (.clk(clk), .D(start_interupt), .Q(d_ff_1_q));  // open: Qn, preset, en, reset
  D_Flip_Flop d_ff_2 (.clk(clk), .D(d_ff_1_q), .Q(d_ff_2_q));  // open: Qn, preset, en, reset
  not not_1 (not_1_out, IE);
  Priority_Encoder #(.select(2)) priority_encoder_1 (
    .in0(1'b1), .in1(one_interupt_request), .in2(two_interupt_request), .in3(two_2_interupt_request),
    .out(int_num));  // open: gs, en_out, en_in
  D_Flip_Flop d_ff_3 (.clk(clk), .D(not_1_out), .Q(d_ff_3_q));  // open: Qn, preset, en, reset
  not not_2 (not_2_out, d_ff_3_q);
  Demultiplexer #(.select(2)) demultiplexer_1 (
    .out1(demultiplexer_1_out1), .out2(demultiplexer_1_out2), .out3(demultiplexer_1_out3), .in(1'b1),
    .sel(int_num));  // open: out0, en
  Register #(.width(2)) register_1 (.D(int_num), .Q(register_1_q), .clk(clk));  // open: en, clr
  Comparator #(.width(2), .mode("unsigned")) comparator_1 (
    .a(int_num), .b(register_1_q), .gt(comparator_1_gt), .lt(comparator_1_lt));  // open: eq
  Multiplexer #(.select(2)) multiplexer_1 (
    .in0(1'b1), .in1(one_exe), .in2(two_exe), .in3(three_exe), .out(multiplexer_1_out), .sel(int_num));  // open: en
  D_Flip_Flop d_ff_4 (.Q(one_exe), .preset(and_1_out), .reset(clear_one));  // open: clk, D, Qn, en
  and and_1 (and_1_out, demultiplexer_1_out1, d_ff_2_q);
  and and_2 (and_2_out, comparator_1_lt, ~multiplexer_1_out);  // AND_Gate
  or or_1 (or_1_out, comparator_1_gt, and_2_out);
  D_Flip_Flop d_ff_5 (.Q(two_exe), .preset(and_3_out), .reset(clear_two));  // open: clk, D, Qn, en
  and and_3 (and_3_out, demultiplexer_1_out2, d_ff_2_q);
  and and_4 (start_interupt, or_1_out, not_2_out);
  D_Flip_Flop d_ff_6 (.Q(three_exe), .preset(and_5_out), .reset(clear_three));  // open: clk, D, Qn, en
  and and_5 (and_5_out, demultiplexer_1_out3, d_ff_2_q);
endmodule

// clk
module pc_reg (
  input  [11:0] W,
  input  clk,
  input  \int ,
  input  eret,
  output [11:0] R
);

  wire [1:0] choose, multiplexer_1_out;
  wire [11:0] ram_1_data;

  Multiplexer #(.select(2), .width(2)) multiplexer_1 (
    .in0(2'b00), .in1(2'b11), .in2(2'b10), .in3(2'b00), .out(multiplexer_1_out), .sel({\int , eret}));  // open: en
  Counter #(.width(2), .max('h3), .trigger("falling")) counter_1 (
    .load(multiplexer_1_out[0]), .count(multiplexer_1_out[1]), .Q(choose), .clk(clk));  // open: D, carry, clr
  RAM #(.addrWidth(2), .dataWidth(12), .bus("separate")) ram_1 (
    .addr(choose), .din(W), .data(ram_1_data), .str(\int ), .clk(clk), .ld(1'b1));  // open: sel, clr
  Register #(.width(12)) register_1 (.D(ram_1_data), .en(1'b1), .Q(R), .clk(clk));  // open: clr
endmodule
