// Logisim project cpu_benchmark.circ as structural Verilog: 1 circuit, main circuit cpu
module cpu (
);

  wire alu_1_p4, ALU_output, and_1_out, and_2_out, and_3_out, and_4_out, and_5_out, beq, blez, bnq, Branch,
       clock_1_out, comparator_1_eq, comparator_1_gt, comparator_1_lt, comparator_2_eq, comparator_2_lt,
       Half_word, halt, not_1_out, or_1_out, or_2_out, or_3_out, PC_MUX_2, PC_MUX_3, RAM_LOAD, RAM_STO, RST,
       syscall, un_Branch, wc, WE;
  wire [1:0] PC_q, Ra, rw, w, Y;
  wire [3:0] ALU_S;
  wire [4:0] multiplexer_3_out, multiplexer_4_out, registerfile_1_p6;
  wire [9:0] PC_q_2;
  wire [15:0] incrementer_1_p2, multiplexer_11_out, rom_1_data, \周期数目 , \总周期数 , \无条件分支指令数 , \有条件分支成功跳转 ,
       \有条件分支指令数 ;
  wire [27:0] bit_extender_2_out, shifter_1_out;
  wire [31:0] adder_1_out, adder_2_out, alu_1_p5, bit_extender_1_out, bit_extender_3_out, bit_extender_4_out,
       bit_extender_5_out, mips_ram_1_p8, multiplexer_2_out, multiplexer_6_out, multiplexer_7_out,
       multiplexer_8_out, multiplexer_9_out, multiplexer_10_out, registerfile_1_p7, registerfile_1_p8,
       shifter_2_out, SyscallOut;
  wire [31:16] rom_1_data_2;

  Button \u_总复位  (.out(RST));
  Register #(.width(12)) PC (.D(multiplexer_10_out[11:0]), .en(halt), .Q({PC_q_2, PC_q}), .clk(clock_1_out), .clr(RST));
  assign bit_extender_1_out = {{20{1'b0}}, {PC_q_2, PC_q}};  // Bit_Extender bit_extender_1
  Clock clock_1 (.out(clock_1_out));
  Hex_Digit_Display hex_digit_display_1 (.value(SyscallOut[27:24]));  // open: dp
  Hex_Digit_Display hex_digit_display_2 (.value(SyscallOut[31:28]));  // open: dp
  Register #(.width(32)) register_1 ();  // open: D, en, Q, clk, clr
  // Incrementer incrementer_1: pin names not known; wires that end beside it: \周期数目 , incrementer_1_p2
  Hex_Digit_Display hex_digit_display_3 (.value(SyscallOut[23:20]));  // open: dp
  Hex_Digit_Display hex_digit_display_4 (.value(SyscallOut[19:16]));  // open: dp
  Adder #(.width(32)) adder_1 (.a(bit_extender_1_out), .b(32'h4), .out(adder_1_out), .cin(1'b0));  // open: cout
  ROM #(.addrWidth(10), .dataWidth(32)) rom_1 (.addr(PC_q_2), .data({rom_1_data_2, rom_1_data}));  // open: sel
  // Probe on rom_1_data
  Counter #(.width(16), .max('hffff)) counter_1 (
    .load(1'b0), .count(halt), .Q(\周期数目 ), .clk(clock_1_out), .clr(RST));  // open: D, carry
  Multiplexer #(.width(16), .enable("false")) multiplexer_1 (
    .in0(incrementer_1_p2), .in1(\周期数目 ), .out(\总周期数 ), .sel(halt));
  Hex_Digit_Display hex_digit_display_5 (.value(SyscallOut[15:12]));  // open: dp
  Hex_Digit_Display hex_digit_display_6 (.value(SyscallOut[11:8]));  // open: dp
  Hex_Digit_Display hex_digit_display_7 (.value(SyscallOut[7:4]));  // open: dp
  Hex_Digit_Display hex_digit_display_8 (.value(SyscallOut[3:0]));  // open: dp
  Multiplexer #(.select(2), .width(32), .enable("false")) multiplexer_2 (
    .in0({alu_1_p5[31:2], wc, alu_1_p5[0]}), .in1(adder_1_out), .in3(multiplexer_8_out),
    .out(multiplexer_2_out), .sel(w));  // open: in2
  controller controller_1 (
    .in_1({rom_1_data_2, rom_1_data}), .Branch(Branch), .rw(rw), .Y(Y), .Half_word(Half_word),
    .un_Branch(un_Branch), .RAM_STO(RAM_STO), .Ra(Ra), .ALU_S(ALU_S), .syscall(syscall), .PC_MUX_2(PC_MUX_2),
    .blez(blez), .WE(WE), .RAM_LOAD(RAM_LOAD), .PC_MUX_3(PC_MUX_3), .bnq(bnq), .w(w), .beq(beq),
    .ALU_output(ALU_output));
  assign bit_extender_2_out = {{2{1'b0}}, {rom_1_data_2[25:16], rom_1_data}};  // Bit_Extender bit_extender_2
  Multiplexer #(.select(2), .width(5), .enable("false")) multiplexer_3 (
    .in0(rom_1_data[15:11]), .in1({5{1'b1}}), .in3(rom_1_data_2[20:16]), .out(multiplexer_3_out), .sel(rw));  // open: in2
  assign bit_extender_3_out = {{16{rom_1_data[15]}}, rom_1_data};  // Bit_Extender bit_extender_3
  // Probe on w
  Counter #(.width(16), .max('hffff)) counter_2 (
    .load(1'b0), .count(un_Branch), .Q(\无条件分支指令数 ), .clk(clock_1_out), .clr(RST));  // open: D, carry
  // Probe on registerfile_1_p6
  // Probe on multiplexer_4_out
  Multiplexer #(.select(2), .width(5), .enable("false")) multiplexer_4 (
    .in0(rom_1_data_2[25:21]), .in1(5'b00010), .in3(rom_1_data_2[20:16]), .out(multiplexer_4_out), .sel(Ra));  // open: in2
  // Probe on \总周期数 
  // Probe on \无条件分支指令数 
  // Probe on \有条件分支指令数 
  // Probe on \有条件分支成功跳转 
  Shifter #(.width(28)) shifter_1 (.in(bit_extender_2_out), .\dist (5'b00010), .out(shifter_1_out));
  // Probe on registerfile_1_p7
  assign bit_extender_4_out = {{27{1'b0}}, rom_1_data[10:6]};  // Bit_Extender bit_extender_4
  // RegisterFile registerfile_1: pin names not known; wires that end beside it: multiplexer_2_out, clock_1_out, WE, multiplexer_3_out, multiplexer_4_out, registerfile_1_p6, registerfile_1_p7, registerfile_1_p8
  Multiplexer #(.select(2), .width(5), .enable("false")) multiplexer_5 (
    .in0(rom_1_data_2[20:16]), .in1(5'b00100), .in3(rom_1_data_2[25:21]), .out(registerfile_1_p6), .sel(Ra));  // open: in2
  // Probe on Ra
  // Probe on multiplexer_8_out
  // Probe on registerfile_1_p8
  Comparator #(.width(32)) comparator_1 (
    .a(registerfile_1_p7), .b(32'ha), .gt(comparator_1_gt), .eq(comparator_1_eq), .lt(comparator_1_lt));
  Counter #(.width(16), .max('hffff)) counter_3 (
    .load(1'b0), .count(Branch), .Q(\有条件分支指令数 ), .clk(clock_1_out), .clr(RST));  // open: D, carry
  Shifter #(.width(32)) shifter_2 (.in(bit_extender_3_out), .\dist (5'b00010), .out(shifter_2_out));
  // Probe on registerfile_1_p7
  // Probe on multiplexer_6_out
  Multiplexer #(.select(2), .width(32), .enable("false")) multiplexer_6 (
    .in0(registerfile_1_p8), .in1(bit_extender_4_out), .in3(bit_extender_3_out), .out(multiplexer_6_out),
    .sel(Y));  // open: in2
  // Probe on ALU_S
  // Probe on Y
  or or_1 (or_1_out, comparator_1_gt, comparator_1_lt);
  Adder #(.width(32)) adder_2 (.a(adder_1_out), .b(shifter_2_out), .out(adder_2_out), .cin(1'b0));  // open: cout
  Comparator #(.width(32)) comparator_2 (
    .a(registerfile_1_p7), .b({32{1'b0}}), .eq(comparator_2_eq), .lt(comparator_2_lt));  // open: gt
  // ALU alu_1: pin names not known; wires that end beside it: registerfile_1_p7, multiplexer_6_out, ALU_S, alu_1_p4, {alu_1_p5[31:2], wc, alu_1_p5[0]}
  Register #(.width(32)) register_2 (
    .D(registerfile_1_p8), .en(and_1_out), .Q(SyscallOut), .clk(clock_1_out), .clr(RST));
  and and_1 (and_1_out, or_1_out, syscall);
  and and_2 (and_2_out, comparator_1_eq, syscall);
  or or_2 (or_2_out, comparator_2_eq, comparator_2_lt);
  not not_1 (not_1_out, alu_1_p4);
  // Probe on {alu_1_p5[31:2], wc, alu_1_p5[0]}
  not not_2 (halt, and_2_out);
  Multiplexer #(.width(32), .enable("false")) multiplexer_7 (
    .in0(adder_1_out), .in1(adder_2_out), .out(multiplexer_7_out), .sel(or_3_out));
  Multiplexer #(.width(32), .enable("false")) multiplexer_8 (
    .in0(mips_ram_1_p8), .in1(bit_extender_5_out), .out(multiplexer_8_out), .sel(Half_word));
  Multiplexer #(.width(32), .enable("false")) multiplexer_9 (
    .in0({adder_1_out[3:0], shifter_1_out}), .in1(multiplexer_7_out), .out(multiplexer_9_out), .sel(PC_MUX_2));
  and and_3 (and_3_out, blez, or_2_out);
  and and_4 (and_4_out, beq, alu_1_p4);
  and and_5 (and_5_out, bnq, not_1_out);
  or or_3 (or_3_out, and_3_out, and_4_out, and_5_out);
  // MIPS_RAM mips_ram_1: pin names not known; wires that end beside it: alu_1_p5[21:2], registerfile_1_p8, RAM_STO, 4'b1111, clock_1_out, RAM_LOAD, RST, mips_ram_1_p8
  Multiplexer #(.width(32), .enable("false")) multiplexer_10 (
    .in0(multiplexer_9_out), .in1(registerfile_1_p7), .out(multiplexer_10_out), .sel(PC_MUX_3));
  Counter #(.width(16), .max('hffff)) counter_4 (
    .load(1'b0), .count(or_3_out), .Q(\有条件分支成功跳转 ), .clk(clock_1_out), .clr(RST));  // open: D, carry
  Multiplexer #(.width(16), .enable("false")) multiplexer_11 (
    .in0(mips_ram_1_p8[15:0]), .in1(mips_ram_1_p8[31:16]), .out(multiplexer_11_out), .sel(wc));
  assign bit_extender_5_out = {{16{multiplexer_11_out[15]}}, multiplexer_11_out};  // Bit_Extender bit_extender_5

  // Notes on the sheet:
  //   数码管输出应该用寄存器锁存，否则显示数据只能一闪而过
  //   可以通过项目增加Logisim库的方式将前几次实验完成的电路作为子电路引入到本电路中使用
  //   contents of rom_1 (hex, n*v repeats v):
  //   20110001 8100005 20110001 20120002 20130003 8100009 20110001 20120002 20130003 810000d 20110001
  //   20120002 20130003 8100011 20110001 20120002 20130003 c1000b8 20100001 20110001 118fc0 112020
  //   20020022 c 118882 12200001 8100015 112020 20020022 c 20110001 118880 112020 20020022 c 12200001
  //   810001f 20110001 118fc0 112020 20020022 c 1188c3 112020 20020022 c 118903 112020 20020022 c 118903
  //   112020 20020022 c 118903 112020 20020022 c 118903 112020 20020022 c 118903 112020 20020022 c 118903
  //   112020 20020022 c 118903 112020 20020022 c 20100001 109fc0 139fc3 8021 2012000c 24160003 26100001
  //   3210000f 20080008 20090001 139900 2709825 132020 20020022 c 1094022 1500fff9 22100001 2018000f
  //   2188024 108700 20080008 20090001 139902 2709825 132021 20020022 c 1094022 1500fff9 108702 2c9b022
  //   12c00001 8100050 4020 1084027 84400 3508ffff 82021 20020022 c 2010ffff 20110000 ae300000 22100001
  //   22310004 ae300000 22100001 22310004 ae300000 22100001 22310004 ae300000 22100001 22310004 ae300000
  //   22100001 22310004 ae300000 22100001 22310004 ae300000 22100001 22310004 ae300000 22100001 22310004
  //   ae300000 22100001 22310004 ae300000 22100001 22310004 ae300000 22100001 22310004 ae300000 22100001
  //   22310004 ae300000 22100001 22310004 ae300000 22100001 22310004 ae300000 22100001 22310004 ae300000
  //   22100001 22310004 22100001 8020 2011003c 8e130000 8e340000 274402a 11000002 ae330000 ae140000
  //   2231fffc 1611fff8 102020 20020022 c 22100004 2011003c 1611fff2 2002000a c 20100000 22100001 102020
  //   20020022 c 22100002 102020 20020022 c 22100003 102020 20020022 c 22100004 102020 20020022 c 22100005
  //   102020 20020022 c 22100006 102020 20020022 c 22100007 102020 20020022 c 22100008 102020 20020022
  //   20020022 c 3e00008
  //   数码管输出
  //   总复位信号应将除ROM以外所有存储组件全部清零
endmodule
