// Logisim project bubble_benchmark.circ as structural Verilog: 12 circuits, main circuit cpu
module cpu (
  input  in_1
);

  wire and_1_out, and_2_out, beq, blez, bnq, Branch_t, clk, comparator_1_eq, comparator_2_eq, condi_suc,
       ctrl_clash, data_clash, half_word_t, halt, halt_g, not_1_out, not_3_out, or_2_out, PC_MUX_2, PC_MUX_3,
       RAM_LOAD, RAM_STO, registerfile_1_p3, RST, syscall_t, un_Branch_t, wb_1_we_out, WE_exe, WE_mem;
  wire [1:0] rA_t, rW_t, word_t;
  wire [4:0] registerfile_1_p4, registerfile_1_p5, registerfile_1_p6, rw_exe, rw_mem;
  wire [7:0] PC_q_2;
  wire [8:0] ex_mem_1_ctrl_msg_out;
  wire [11:0] adder_1_out, id_ex_1_pc_4_out, if_id_1_pc_4_out, multiplexer_1_out, npc_1_out_7, PC_4, PC_q;
  wire [14:0] controller_1_y, id_ex_1_ctrl_msg_out;
  wire [15:0] \总周期数 , \无条件分支指令数 , \有条件分支成功跳转 , \有条件分支指令数 ;
  wire [31:0] A, alu_1_p4, B, bit_extender_1_out, ex_mem_1_a_out, ex_mem_1_alu_out, ex_mem_1_b_out,
       ex_mem_1_instruction_out, id_ex_1_a_out, id_ex_1_b_out, id_ex_1_instruction_out,
       if_id_1_instruction_out, mips_ram_1_p8, multiplexer_4_out, registerfile_1_p1, rom_1_data, SyscallOut,
       wb_1_a_out, word_ctrl_1_out_4, y_ctrl_1_out_4;

  Button \u_总复位  (.out(RST));
  Register #(.width(12)) PC (
    .D(multiplexer_1_out), .en(and_1_out), .Q({PC_q[11:10], PC_q_2, PC_q[1:0]}), .clk(clk), .clr(RST));
  // OR_Gate or_1 is placed but not wired
  Hex_Digit_Display hex_digit_display_1 (.value(SyscallOut[27:24]));  // open: dp
  Hex_Digit_Display hex_digit_display_2 (.value(SyscallOut[31:28]));  // open: dp
  and and_1 (and_1_out, halt, not_1_out);
  not not_1 (not_1_out, data_clash);
  or or_2 (or_2_out, ctrl_clash, data_clash);
  Clock clock_1 (.out(clk));
  Hex_Digit_Display hex_digit_display_3 (.value(SyscallOut[23:20]));  // open: dp
  Hex_Digit_Display hex_digit_display_4 (.value(SyscallOut[19:16]));  // open: dp
  Adder #(.width(12)) adder_1 (
    .a({PC_q[11:10], PC_q_2, PC_q[1:0]}), .b(12'h4), .out(adder_1_out), .cin(1'b0));  // open: cout
  ROM #(.dataWidth(32)) rom_1 (.addr(PC_q_2), .data(rom_1_data));  // open: sel
  Counter counter_1 (.count(or_2_out), .clk(clk));  // open: load, D, Q, carry, clr
  Hex_Digit_Display hex_digit_display_5 (.value(SyscallOut[15:12]));  // open: dp
  Hex_Digit_Display hex_digit_display_6 (.value(SyscallOut[11:8]));  // open: dp
  // Probe on adder_1_out
  Hex_Digit_Display hex_digit_display_7 (.value(SyscallOut[3:0]));  // open: dp
  Hex_Digit_Display hex_digit_display_8 (.value(SyscallOut[7:4]));  // open: dp
  // Probe on npc_1_out_7
  not not_2 (ctrl_clash, comparator_1_eq);
  not not_3 (not_3_out, data_clash);
  Multiplexer #(.width(12), .enable("false")) multiplexer_1 (
    .in0(npc_1_out_7), .in1(adder_1_out), .out(multiplexer_1_out), .sel(comparator_1_eq));
  IF_ID if_id_1 (
    .pc_4(adder_1_out), .CLK(clk), .pc_4_out(if_id_1_pc_4_out), .\同步清零 (ctrl_clash), .\通行 (not_3_out),
    .instruction(rom_1_data), .instruction_out(if_id_1_instruction_out));
  // Probe on \总周期数 
  // Probe on \无条件分支指令数 
  // Probe on \有条件分支指令数 
  // Probe on \有条件分支成功跳转 
  controller controller_1 (
    .in_1(if_id_1_instruction_out), .Branch(Branch_t), .rw(controller_1_y[13:12]), .Y(controller_1_y[1:0]),
    .Half_word(controller_1_y[2]), .un_Branch(un_Branch_t), .RAM_STO(controller_1_y[3]), .Ra(rA_t),
    .ALU_S(controller_1_y[7:4]), .syscall(syscall_t), .PC_MUX_2(PC_MUX_2), .blez(blez),
    .WE(controller_1_y[9]), .RAM_LOAD(controller_1_y[14]), .PC_MUX_3(PC_MUX_3), .bnq(bnq),
    .w(controller_1_y[11:10]), .beq(beq));  // open: ALU_output
  condi_jump condi_jump_1 (.A(A), .out_6(condi_suc), .B(B), .blez(blez), .beq(beq), .bnq(bnq));
  // Probe on if_id_1_instruction_out
  npc npc_1 (
    .in_1(if_id_1_instruction_out), .in_2(if_id_1_pc_4_out), .out_7(npc_1_out_7), .in_3(condi_suc),
    .in_4(PC_MUX_2), .in_5(PC_MUX_3), .in_6(A));
  statistic statistic_1 (
    .out_11(\总周期数 ), .A(A), .out_12(\无条件分支指令数 ), .out_13(\有条件分支指令数 ), .B(B), .out_14(\有条件分支成功跳转 ),
    .in_7(clk), .in_8(RST), .syscall_t(syscall_t), .out_15(SyscallOut), .condi_suc(condi_suc),
    .un_branch_t(un_Branch_t), .branch_t(Branch_t), .out_16(halt_g), .in_5(halt), .in_6(data_clash));
  Comparator #(.width(12)) comparator_1 (.a(if_id_1_pc_4_out), .b(npc_1_out_7), .eq(comparator_1_eq));  // open: gt, lt
  data_clash data_clash_1 (
    .rA(registerfile_1_p6), .out_7(data_clash), .rB(registerfile_1_p5), .rw(rw_exe), .rw_2(rw_mem),
    .WE_rw(WE_exe), .WE_rw_2(WE_mem));
  // Probe on {controller_1_y[14:9], syscall_t, controller_1_y[7:0]}
  // RegisterFile registerfile_1: pin names not known; wires that end beside it: registerfile_1_p1, clk, registerfile_1_p3, registerfile_1_p4, registerfile_1_p5, registerfile_1_p6, A, B
  // Probe on registerfile_1_p5
  // Probe on registerfile_1_p6
  read_reg_ctrl read_reg_ctrl_1 (
    .in_1(if_id_1_instruction_out), .in_2(rA_t), .out_3(registerfile_1_p5), .out_4(registerfile_1_p6));
  // Probe on registerfile_1_p4
  // Probe on B
  // Probe on A
  // Probe on registerfile_1_p1
  ID_EX id_ex_1 (
    .pc_4(if_id_1_pc_4_out), .pc_4_out(id_ex_1_pc_4_out), .instruction(if_id_1_instruction_out),
    .instruction_out(id_ex_1_instruction_out), .CLK(clk), .\同步清零 (data_clash), .\通行 (halt),
    .ctrl_msg({controller_1_y[14:9], syscall_t, controller_1_y[7:0]}),
    .ctrl_msg_out({id_ex_1_ctrl_msg_out[14:10], WE_exe, id_ex_1_ctrl_msg_out[8:0]}), .A(A),
    .A_out(id_ex_1_a_out), .B(B), .B_out(id_ex_1_b_out));
  // Probe on id_ex_1_instruction_out
  // Probe on {id_ex_1_ctrl_msg_out[14:10], WE_exe, id_ex_1_ctrl_msg_out[8:0]}
  Y_ctrl y_ctrl_1 (
    .in_1(id_ex_1_instruction_out), .out_4(y_ctrl_1_out_4), .in_2(id_ex_1_b_out),
    .in_3(id_ex_1_ctrl_msg_out[1:0]));
  Multiplexer #(.select(2), .width(5), .enable("false")) multiplexer_2 (
    .in0(id_ex_1_instruction_out[15:11]), .in1({5{1'b1}}), .in3(id_ex_1_instruction_out[20:16]),
    .out(rw_exe), .sel(id_ex_1_ctrl_msg_out[13:12]));  // open: in2
  // ALU alu_1: pin names not known; wires that end beside it: id_ex_1_a_out, y_ctrl_1_out_4, id_ex_1_ctrl_msg_out[7:4], alu_1_p4, alu_1_p4, id_ex_1_b_out
  EX_MEM ex_mem_1 (
    .pc_4(id_ex_1_pc_4_out), .pc_4_out(PC_4), .instruction(id_ex_1_instruction_out),
    .instruction_out(ex_mem_1_instruction_out),
    .ctrl_msg({id_ex_1_ctrl_msg_out[14:10], WE_exe, id_ex_1_ctrl_msg_out[8:0]}),
    .ctrl_msg_out({RAM_LOAD, rW_t, word_t, WE_mem, ex_mem_1_ctrl_msg_out[8:4], RAM_STO, half_word_t, ex_mem_1_ctrl_msg_out[1:0]}),
    .alu(alu_1_p4), .alu_out(ex_mem_1_alu_out), .CLK(clk), .\同步清零 (1'b0), .\通行 (halt), .B(id_ex_1_b_out),
    .B_out(ex_mem_1_b_out), .A(id_ex_1_a_out), .A_out(ex_mem_1_a_out));
  // Probe on ex_mem_1_instruction_out
  // MIPS_RAM mips_ram_1: pin names not known; wires that end beside it: ex_mem_1_alu_out[21:2], ex_mem_1_b_out, RAM_STO, 4'b1111, clk, RAM_LOAD, RST, mips_ram_1_p8, ex_mem_1_instruction_out[25:21]
  Multiplexer #(.select(2), .width(5), .enable("false")) multiplexer_3 (
    .in0(ex_mem_1_instruction_out[15:11]), .in1({5{1'b1}}), .in3(ex_mem_1_instruction_out[20:16]),
    .out(rw_mem), .sel(rW_t));  // open: in2
  assign bit_extender_1_out = {{20{1'b0}}, PC_4};  // Bit_Extender bit_extender_1
  word_ctrl word_ctrl_1 (
    .out_4(word_ctrl_1_out_4), .in_1(ex_mem_1_alu_out[1]), .in_2(half_word_t), .in_3(mips_ram_1_p8));
  Multiplexer #(.select(2), .width(32), .enable("false")) multiplexer_4 (
    .in0(ex_mem_1_alu_out), .in1(bit_extender_1_out), .in3(word_ctrl_1_out_4), .out(multiplexer_4_out),
    .sel(word_t));  // open: in2
  // Probe on multiplexer_4_out
  WB wb_1 (
    .halt(WE_mem), .RW(rw_mem), .w(multiplexer_4_out), .CLK(clk), .halt_out(registerfile_1_p3),
    .rw_out(registerfile_1_p4), .w_out(registerfile_1_p1), .\同步清零 (1'b0), .\通行 (halt),
    .WE(ex_mem_1_ctrl_msg_out[8]), .WE_out(wb_1_we_out), .A(ex_mem_1_a_out), .A_out(wb_1_a_out));
  Comparator #(.width(32)) comparator_2 (.a(wb_1_a_out), .b(32'ha), .eq(comparator_2_eq));  // open: gt, lt
  not not_4 (halt, and_2_out);
  and and_2 (and_2_out, comparator_2_eq, wb_1_we_out);

  // Notes on the sheet:
  //   数码管输出应该用寄存器锁存，否则显示数据只能一闪而过
  //   可以通过项目增加Logisim库的方式将前几次实验完成的电路作为子电路引入到本电路中使用
  //   contents of rom_1 (hex, n*v repeats v):
  //   20110001 8000c05 20110001 20120002 20130003 8000c09 20110001 20120002 20130003 8000c0d 20110001
  //   20120002 20130003 8000c11 20110001 20120002 20130003 c000cb8 20100001 20110001 118fc0 112020
  //   20020022 c 118882 12200001 8000c15 112020 20020022 c 20110001 118880 112020 20020022 c 12200001
  //   8000c1f 20110001 118fc0 112020 20020022 c 1188c3 112020 20020022 c 118903 112020 20020022 c 118903
  //   112020 20020022 c 118903 112020 20020022 c 118903 112020 20020022 c 118903 112020 20020022 c 118903
  //   112020 20020022 c 118903 112020 20020022 c 20100001 109fc0 139fc3 8021 2012000c 24160003 26100001
  //   3210000f 20080008 20090001 139900 2709825 132020 20020022 c 1094022 1500fff9 22100001 2018000f
  //   2188024 108700 20080008 20090001 139902 2709825 132021 20020022 c 1094022 1500fff9 108702 2c9b022
  //   12c00001 8000c50 4020 1084027 84400 3508ffff 82021 20020022 c 2010ffff 20110000 ae300000 22100001
  //   22310004 ae300000 22100001 22310004 ae300000 22100001 22310004 ae300000 22100001 22310004 ae300000
  //   22100001 22310004 ae300000 22100001 22310004 ae300000 22100001 22310004 ae300000 22100001 22310004
  //   ae300000 22100001 22310004 ae300000 22100001 22310004 ae300000 22100001 22310004 ae300000 22100001
  //   22310004 ae300000 22100001 22310004 ae300000 22100001 22310004 ae300000 22100001 22310004 ae300000
  //   22100001 22310004 22100001 8020 2011003c 8e130000 8e340000 274402a 11000002 ae330000 ae140000
  //   2231fffc 1611fff8 102020 20020022 c 22100004 2011003c 1611fff2 2002000a c 20100000 22100001 102020
  //   20020022 c 22100002 102020 20020022 c 22100003 102020 20020022 c 22100004 102020 20020022 c 22100005
  //   102020 20020022 c 22100006 102020 20020022 c 22100007 102020 20020022 c 22100008 102020 20020022
  //   20020022 c 3e00008
  //   数码管输出
  //   总复位信号应将除ROM以外所有存储组件全部清零
endmodule

module condi_jump (
  input  [31:0] A,
  input  blez,
  input  beq,
  input  [31:0] B,
  input  bnq,
  output out_6
);

  wire and_1_out, and_2_out, and_3_out, comparator_1_eq, comparator_2_eq, comparator_2_lt, not_1_out,
       or_1_out;

  Comparator #(.width(32)) comparator_1 (.a(A), .b(B), .eq(comparator_1_eq));  // open: gt, lt
  Comparator #(.width(32)) comparator_2 (
    .a(A), .b({32{1'b0}}), .eq(comparator_2_eq), .lt(comparator_2_lt));  // open: gt
  or or_1 (or_1_out, comparator_2_eq, comparator_2_lt);
  not not_1 (not_1_out, comparator_1_eq);
  and and_1 (and_1_out, blez, or_1_out);
  and and_2 (and_2_out, beq, comparator_1_eq);
  and and_3 (and_3_out, bnq, not_1_out);
  or or_2 (out_6, and_1_out, and_2_out, and_3_out);

  // Other names for the same wires on the sheet: condi_suc = out_6
endmodule

module npc (
  input  [31:0] in_1,
  input  [11:0] in_2,
  input  in_3,
  input  in_4,
  input  in_5,
  input  [31:0] in_6,
  output [11:0] out_7
);

  wire [27:0] bit_extender_2_out, shifter_1_out;
  wire [31:0] adder_1_out, bit_extender_1_out, bit_extender_3_out, multiplexer_1_out, multiplexer_2_out,
       shifter_2_out;
  wire [31:12] multiplexer_3_out;

  assign bit_extender_1_out = {{20{1'b0}}, in_2};  // Bit_Extender bit_extender_1
  assign bit_extender_2_out = {{2{1'b0}}, in_1[25:0]};  // Bit_Extender bit_extender_2
  assign bit_extender_3_out = {{16{in_1[15]}}, in_1[15:0]};  // Bit_Extender bit_extender_3
  Shifter #(.width(28)) shifter_1 (.in(bit_extender_2_out), .\dist (5'b00010), .out(shifter_1_out));
  Shifter #(.width(32)) shifter_2 (.in(bit_extender_3_out), .\dist (5'b00010), .out(shifter_2_out));
  Adder #(.width(32)) adder_1 (.a(bit_extender_1_out), .b(shifter_2_out), .out(adder_1_out), .cin(1'b0));  // open: cout
  Multiplexer #(.width(32), .enable("false")) multiplexer_1 (
    .in0(bit_extender_1_out), .in1(adder_1_out), .out(multiplexer_1_out), .sel(in_3));
  Multiplexer #(.width(32), .enable("false")) multiplexer_2 (
    .in0({bit_extender_1_out[3:0], shifter_1_out}), .in1(multiplexer_1_out), .out(multiplexer_2_out),
    .sel(in_4));
  Multiplexer #(.width(32), .enable("false")) multiplexer_3 (
    .in0(multiplexer_2_out), .in1(in_6), .out({multiplexer_3_out, out_7}), .sel(in_5));

  // Other names for the same wires on the sheet: npc[11:0] = out_7; A[31:0] = in_6; condi_suc = in_3;
  //   instruction[31:0] = in_1; pc_4[11:0] = in_2; PC_MUX_2 = in_4; PC_MUX_3 = in_5
endmodule

module statistic (
  input  un_branch_t,
  input  [31:0] A,
  input  branch_t,
  input  [31:0] B,
  input  in_5,
  input  in_6,
  input  in_7,
  input  in_8,
  input  syscall_t,
  input  condi_suc,
  output [15:0] out_11,
  output [15:0] out_12,
  output [15:0] out_13,
  output [15:0] out_14,
  output [31:0] out_15,
  output out_16
);

  wire and_2_out, and_3_out, and_4_out, and_5_out, and_6_out, comparator_1_eq, comparator_1_gt,
       comparator_1_lt, not_1_out, or_1_out, stop_count;
  wire [15:0] incrementer_1_p2, \周期数目 ;

  Counter #(.width(16), .max('hffff)) counter_1 (
    .load(1'b0), .count(in_5), .Q(\周期数目 ), .clk(in_7), .clr(in_8));  // open: D, carry
  and and_1 (stop_count, in_5, not_1_out);
  not not_1 (not_1_out, in_6);
  Counter #(.width(16), .max('hffff)) counter_2 (
    .load(1'b0), .count(and_2_out), .Q(out_12), .clk(in_7), .clr(in_8));  // open: D, carry
  and and_2 (and_2_out, un_branch_t, stop_count);
  Counter #(.width(16), .max('hffff)) counter_3 (
    .load(1'b0), .count(and_3_out), .Q(out_13), .clk(in_7), .clr(in_8));  // open: D, carry
  and and_3 (and_3_out, branch_t, stop_count);
  Counter #(.width(16), .max('hffff)) counter_4 (
    .load(1'b0), .count(and_4_out), .Q(out_14), .clk(in_7), .clr(in_8));  // open: D, carry
  and and_4 (and_4_out, condi_suc, stop_count);
  Comparator #(.width(32)) comparator_1 (
    .a(A), .b(32'ha), .gt(comparator_1_gt), .eq(comparator_1_eq), .lt(comparator_1_lt));
  or or_1 (or_1_out, comparator_1_gt, comparator_1_lt);
  Register #(.width(32)) register_1 (.D(B), .en(and_5_out), .Q(out_15), .clk(in_7), .clr(in_8));
  and and_5 (and_5_out, or_1_out, syscall_t);
  and and_6 (and_6_out, comparator_1_eq, syscall_t);
  not not_2 (out_16, and_6_out);
  // Incrementer incrementer_1: pin names not known; wires that end beside it: \周期数目 , incrementer_1_p2
  Multiplexer #(.width(16), .enable("false")) multiplexer_1 (
    .in0(incrementer_1_p2), .in1(\周期数目 ), .out(out_11), .sel(in_5));

  // Other names for the same wires on the sheet: clk = in_7; condi_num[15:0] = out_13; condi_suc_num[15:0] = out_14;
  //   data_clash = in_6; halt = out_16; rst = in_8; strong_halt = in_5; SyscallOut[31:0] = out_15;
  //   total_cycles[15:0] = out_11; uncondi_num[15:0] = out_12
endmodule

// Y_t
module Y_ctrl (
  input  [31:0] in_1,
  input  [31:0] in_2,
  input  [1:0] in_3,
  output [31:0] out_4
);

  wire [31:0] bit_extender_1_out, bit_extender_2_out;

  assign bit_extender_1_out = {{16{in_1[15]}}, in_1[15:0]};  // Bit_Extender bit_extender_1
  assign bit_extender_2_out = {{27{1'b0}}, in_1[10:6]};  // Bit_Extender bit_extender_2
  Multiplexer #(.select(2), .width(32), .enable("false")) multiplexer_1 (
    .in0(in_2), .in1(bit_extender_2_out), .in3(bit_extender_1_out), .out(out_4), .sel(in_3));  // open: in2

  // Other names for the same wires on the sheet: B[31:0] = in_2; instruction[31:0] = in_1; Y[31:0] = out_4;
  //   Y_t[1:0] = in_3
endmodule

module word_ctrl (
  input  in_1,
  input  in_2,
  input  [31:0] in_3,
  output [31:0] out_4
);

  wire [15:0] multiplexer_1_out;
  wire [31:0] bit_extender_1_out;

  Multiplexer #(.width(16), .enable("false")) multiplexer_1 (
    .in0(in_3[15:0]), .in1(in_3[31:16]), .out(multiplexer_1_out), .sel(in_1));
  Multiplexer #(.width(32), .enable("false")) multiplexer_2 (
    .in0(in_3), .in1(bit_extender_1_out), .out(out_4), .sel(in_2));
  assign bit_extender_1_out = {{16{multiplexer_1_out[15]}}, multiplexer_1_out};  // Bit_Extender bit_extender_1

  // Other names for the same wires on the sheet: D[31:0] = in_3; D_out[31:0] = out_4; half_word_t = in_2; wc = in_1
endmodule

module read_reg_ctrl (
  input  [31:0] in_1,
  input  [1:0] in_2,
  output [4:0] out_3,
  output [4:0] out_4
);

  Multiplexer #(.select(2), .width(5), .enable("false")) multiplexer_1 (
    .in0(in_1[25:21]), .in1(5'b00010), .in3(in_1[20:16]), .out(out_3), .sel(in_2));  // open: in2
  Multiplexer #(.select(2), .width(5), .enable("false")) multiplexer_2 (
    .in0(in_1[20:16]), .in1(5'b00100), .in3(in_1[25:21]), .out(out_4), .sel(in_2));  // open: in2

  // Other names for the same wires on the sheet: instruction[31:0] = in_1; rA[4:0] = out_3; rA_t[1:0] = in_2;
  //   rB[4:0] = out_4

  // Notes on the sheet:
  //   输入
  //   输出
endmodule

module data_clash (
  input  [4:0] rA,
  input  [4:0] rB,
  input  [4:0] rw,
  input  WE_rw,
  input  [4:0] rw_2,
  input  WE_rw_2,
  output out_7
);

  wire and_1_out, and_2_out, comparator_1_eq, comparator_2_eq, comparator_3_eq, comparator_4_eq,
       comparator_5_eq, comparator_6_eq, not_1_out, not_2_out, or_1_out, or_2_out;

  Comparator #(.width(5)) comparator_1 (.a(rA), .b(rw), .eq(comparator_1_eq));  // open: gt, lt
  Comparator #(.width(5)) comparator_2 (.a(rB), .b(rw), .eq(comparator_2_eq));  // open: gt, lt
  Comparator #(.width(5)) comparator_3 (.a(rA), .b(rw_2), .eq(comparator_3_eq));  // open: gt, lt
  Comparator #(.width(5)) comparator_4 (.a(rB), .b(rw_2), .eq(comparator_4_eq));  // open: gt, lt
  Comparator #(.width(5)) comparator_5 (.a(rw), .b({5{1'b0}}), .eq(comparator_5_eq));  // open: gt, lt
  Comparator #(.width(5)) comparator_6 (.a(rw_2), .b({5{1'b0}}), .eq(comparator_6_eq));  // open: gt, lt
  not not_1 (not_1_out, comparator_5_eq);
  not not_2 (not_2_out, comparator_6_eq);
  or or_1 (or_1_out, comparator_1_eq, comparator_2_eq);
  or or_2 (or_2_out, comparator_3_eq, comparator_4_eq);
  and and_1 (and_1_out, not_1_out, WE_rw, or_1_out);
  and and_2 (and_2_out, not_2_out, WE_rw_2, or_2_out);
  or or_3 (out_7, and_1_out, and_2_out);

  // Other names for the same wires on the sheet: is_clash = out_7; rw_exe[4:0] = rw; rw_mem[4:0] = rw_2;
  //   WE_exe = WE_rw; WE_mem = WE_rw_2
endmodule

module IF_ID (
  input  [11:0] pc_4,
  input  [31:0] instruction,
  input  CLK,
  input  \同步清零 ,
  input  \通行 ,
  output [11:0] pc_4_out,
  output [31:0] instruction_out
);

  wire [11:0] multiplexer_1_out;
  wire [31:0] multiplexer_2_out;

  Multiplexer #(.width(12), .enable("false")) multiplexer_1 (
    .in0(pc_4), .in1({12{1'b0}}), .out(multiplexer_1_out), .sel(\同步清零 ));
  Multiplexer #(.width(32), .enable("false")) multiplexer_2 (
    .in0(instruction), .in1({32{1'b0}}), .out(multiplexer_2_out), .sel(\同步清零 ));
  Register #(.width(12)) register_1 (.D(multiplexer_1_out), .en(\通行 ), .Q(pc_4_out), .clk(CLK));  // open: clr
  Register #(.width(32)) register_2 (.D(multiplexer_2_out), .en(\通行 ), .Q(instruction_out), .clk(CLK));  // open: clr
endmodule

module ID_EX (
  input  [11:0] pc_4,
  input  [31:0] instruction,
  input  [14:0] ctrl_msg,
  input  [31:0] A,
  input  [31:0] B,
  input  CLK,
  input  \同步清零 ,
  input  \通行 ,
  output [11:0] pc_4_out,
  output [31:0] instruction_out,
  output [14:0] ctrl_msg_out,
  output [31:0] A_out,
  output [31:0] B_out
);

  wire [11:0] multiplexer_1_out;
  wire [14:0] multiplexer_3_out;
  wire [31:0] multiplexer_2_out, multiplexer_4_out, multiplexer_5_out;

  Multiplexer #(.width(12), .enable("false")) multiplexer_1 (
    .in0(pc_4), .in1({12{1'b0}}), .out(multiplexer_1_out), .sel(\同步清零 ));
  Multiplexer #(.width(32), .enable("false")) multiplexer_2 (
    .in0(instruction), .in1({32{1'b0}}), .out(multiplexer_2_out), .sel(\同步清零 ));
  Multiplexer #(.width(15), .enable("false")) multiplexer_3 (
    .in0(ctrl_msg), .in1({15{1'b0}}), .out(multiplexer_3_out), .sel(\同步清零 ));
  Multiplexer #(.width(32), .enable("false")) multiplexer_4 (
    .in0(A), .in1({32{1'b0}}), .out(multiplexer_4_out), .sel(\同步清零 ));
  Multiplexer #(.width(32), .enable("false")) multiplexer_5 (
    .in0(B), .in1({32{1'b0}}), .out(multiplexer_5_out), .sel(\同步清零 ));
  Register #(.width(12)) register_1 (.D(multiplexer_1_out), .en(\通行 ), .Q(pc_4_out), .clk(CLK));  // open: clr
  Register #(.width(32)) register_2 (.D(multiplexer_2_out), .en(\通行 ), .Q(instruction_out), .clk(CLK));  // open: clr
  Register #(.width(15)) register_3 (.D(multiplexer_3_out), .en(\通行 ), .Q(ctrl_msg_out), .clk(CLK));  // open: clr
  Register #(.width(32)) register_4 (.D(multiplexer_4_out), .en(\通行 ), .Q(A_out), .clk(CLK));  // open: clr
  Register #(.width(32)) register_5 (.D(multiplexer_5_out), .en(\通行 ), .Q(B_out), .clk(CLK));  // open: clr
endmodule

module EX_MEM (
  input  [11:0] pc_4,
  input  [31:0] instruction,
  input  [14:0] ctrl_msg,
  input  [31:0] alu,
  input  [31:0] B,
  input  [31:0] A,
  input  CLK,
  input  \同步清零 ,
  input  \通行 ,
  output [11:0] pc_4_out,
  output [31:0] instruction_out,
  output [14:0] ctrl_msg_out,
  output [31:0] alu_out,
  output [31:0] B_out,
  output [31:0] A_out
);

  wire [11:0] multiplexer_1_out;
  wire [14:0] multiplexer_3_out;
  wire [31:0] multiplexer_2_out, multiplexer_4_out, multiplexer_5_out, multiplexer_6_out;

  Multiplexer #(.width(12), .enable("false")) multiplexer_1 (
    .in0(pc_4), .in1({12{1'b0}}), .out(multiplexer_1_out), .sel(\同步清零 ));
  Multiplexer #(.width(32), .enable("false")) multiplexer_2 (
    .in0(instruction), .in1({32{1'b0}}), .out(multiplexer_2_out), .sel(\同步清零 ));
  Multiplexer #(.width(15), .enable("false")) multiplexer_3 (
    .in0(ctrl_msg), .in1({15{1'b0}}), .out(multiplexer_3_out), .sel(\同步清零 ));
  Multiplexer #(.width(32), .enable("false")) multiplexer_4 (
    .in0(alu), .in1({32{1'b0}}), .out(multiplexer_4_out), .sel(\同步清零 ));
  Multiplexer #(.width(32), .enable("false")) multiplexer_5 (
    .in0(B), .in1({32{1'b0}}), .out(multiplexer_5_out), .sel(\同步清零 ));
  Multiplexer #(.width(32), .enable("false")) multiplexer_6 (
    .in0(A), .in1({32{1'b0}}), .out(multiplexer_6_out), .sel(\同步清零 ));
  Register #(.width(12)) register_1 (.D(multiplexer_1_out), .en(\通行 ), .Q(pc_4_out), .clk(CLK));  // open: clr
  Register #(.width(32)) register_2 (.D(multiplexer_2_out), .en(\通行 ), .Q(instruction_out), .clk(CLK));  // open: clr
  Register #(.width(15)) register_3 (.D(multiplexer_3_out), .en(\通行 ), .Q(ctrl_msg_out), .clk(CLK));  // open: clr
  Register #(.width(32)) register_4 (.D(multiplexer_4_out), .en(\通行 ), .Q(alu_out), .clk(CLK));  // open: clr
  Register #(.width(32)) register_5 (.D(multiplexer_5_out), .en(\通行 ), .Q(B_out), .clk(CLK));  // open: clr
  Register #(.width(32)) register_6 (.D(multiplexer_6_out), .en(\通行 ), .Q(A_out), .clk(CLK));  // open: clr
endmodule

module WB (
  input  halt,
  input  WE,
  input  [4:0] RW,
  input  [31:0] w,
  input  [31:0] A,
  input  CLK,
  input  \同步清零 ,
  input  \通行 ,
  output halt_out,
  output WE_out,
  output [4:0] rw_out,
  output [31:0] w_out,
  output [31:0] A_out
);

  wire multiplexer_1_out, multiplexer_2_out;
  wire [4:0] multiplexer_3_out;
  wire [31:0] multiplexer_4_out, multiplexer_5_out;

  Multiplexer #(.enable("false")) multiplexer_1 (.in0(halt), .in1(1'b0), .out(multiplexer_1_out), .sel(\同步清零 ));
  Multiplexer #(.enable("false")) multiplexer_2 (.in0(WE), .in1(1'b0), .out(multiplexer_2_out), .sel(\同步清零 ));
  Multiplexer #(.width(5), .enable("false")) multiplexer_3 (
    .in0(RW), .in1({5{1'b0}}), .out(multiplexer_3_out), .sel(\同步清零 ));
  Multiplexer #(.width(32), .enable("false")) multiplexer_4 (
    .in0(w), .in1({32{1'b0}}), .out(multiplexer_4_out), .sel(\同步清零 ));
  Multiplexer #(.width(32), .enable("false")) multiplexer_5 (
    .in0(A), .in1({32{1'b0}}), .out(multiplexer_5_out), .sel(\同步清零 ));
  Register #(.width(1)) register_1 (.D(multiplexer_1_out), .en(\通行 ), .Q(halt_out), .clk(CLK));  // open: clr
  Register #(.width(1)) register_2 (.D(multiplexer_2_out), .en(\通行 ), .Q(WE_out), .clk(CLK));  // open: clr
  Register #(.width(5)) register_3 (.D(multiplexer_3_out), .en(\通行 ), .Q(rw_out), .clk(CLK));  // open: clr
  Register #(.width(32)) register_4 (.D(multiplexer_4_out), .en(\通行 ), .Q(w_out), .clk(CLK));  // open: clr
  Register #(.width(32)) register_5 (.D(multiplexer_5_out), .en(\通行 ), .Q(A_out), .clk(CLK));  // open: clr
endmodule
