// Logisim project controller.circ as structural Verilog
module controller (
  input  [31:0] in_1,
  output Branch,
  output [1:0] rw,
  output [1:0] Y,
  output Half_word,
  output un_Branch,
  output RAM_STO,
  output [1:0] Ra,
  output [3:0] ALU_S,
  output syscall,
  output PC_MUX_2,
  output blez,
  output WE,
  output RAM_LOAD,
  output PC_MUX_3,
  output bnq,
  output [1:0] w,
  output beq,
  output ALU_output
);

  wire or_1_out;
  wire [6:0] \input ;

  Multiplexer #(.width(6), .enable("false")) multiplexer_1 (
    .in0(in_1[31:26]), .in1(in_1[5:0]),
    .out({\input [1], \input [2], \input [3], \input [4], \input [5], \input [6]}), .sel(\input [0]));
  or or_1 (or_1_out, in_1[28], in_1[26], in_1[27], in_1[29], in_1[30], in_1[31]);
  not not_1 (\input [0], or_1_out);
  rw u_rw (
    .is_funct(\input [0]), .funct6(\input [1]), .funct5(\input [2]), .funct4(\input [3]),
    .funct3(\input [4]), .funct2(\input [5]), .funct1(\input [6]), .rw_0(rw[0]), .rw_1(rw[1]));
  Ra u_Ra (
    .is_funct(\input [0]), .funct6(\input [1]), .funct5(\input [2]), .funct4(\input [3]),
    .funct3(\input [4]), .funct2(\input [5]), .funct1(\input [6]), .Ra_0(Ra[0]), .Ra_1(Ra[1]));
  WE u_WE (
    .is_funct(\input [0]), .funct6(\input [1]), .funct5(\input [2]), .funct4(\input [3]),
    .funct3(\input [4]), .funct2(\input [5]), .funct1(\input [6]), .WE(WE));
  summary summary (
    .is_funct(\input [0]), .funct6(\input [1]), .funct5(\input [2]), .funct4(\input [3]),
    .funct3(\input [4]), .funct2(\input [5]), .funct1(\input [6]), .blez(blez), .beq(beq), .bnq(bnq),
    .RAM_STO(RAM_STO), .RAM_LOAD(RAM_LOAD), .Half_word(Half_word), .Branch(Branch), .un_Branch(un_Branch));
  ALU_S u_ALU_S (
    .is_funct(\input [0]), .funct6(\input [1]), .funct5(\input [2]), .funct4(\input [3]),
    .funct3(\input [4]), .funct2(\input [5]), .funct1(\input [6]), .ALU_S_4(ALU_S[3]), .ALI_S_3(ALU_S[2]),
    .ALI_S_2(ALU_S[1]), .ALI_S_1(ALU_S[0]));
  w u_w (
    .is_funct(\input [0]), .funct6(\input [1]), .funct5(\input [2]), .funct4(\input [3]),
    .funct3(\input [4]), .funct2(\input [5]), .funct1(\input [6]), .w_0(w[0]), .w_1(w[1]));
  Y u_Y (
    .is_funct(\input [0]), .funct6(\input [1]), .funct5(\input [2]), .funct4(\input [3]),
    .funct3(\input [4]), .funct2(\input [5]), .funct1(\input [6]), .Y_0(Y[0]), .Y_1(Y[1]));
  PC_MUX_2 u_PC_MUX_2 (
    .is_funct(\input [0]), .funct6(\input [1]), .funct5(\input [2]), .funct4(\input [3]),
    .funct3(\input [4]), .funct2(\input [5]), .funct1(\input [6]), .PC_MUX_2(PC_MUX_2));
  PC_MUX_3 u_PC_MUX_3 (
    .is_funct(\input [0]), .funct6(\input [1]), .funct5(\input [2]), .funct4(\input [3]),
    .funct3(\input [4]), .funct2(\input [5]), .funct1(\input [6]), .PC_MUX_3(PC_MUX_3));
  syscall syscall_1 (
    .is_funct(\input [0]), .funct6(\input [1]), .funct5(\input [2]), .funct4(\input [3]),
    .funct3(\input [4]), .funct2(\input [5]), .funct1(\input [6]), .syscall(syscall));
  ALU_output u_ALU_output (
    .is_funct(\input [0]), .funct6(\input [1]), .funct5(\input [2]), .funct4(\input [3]),
    .funct3(\input [4]), .funct2(\input [5]), .funct1(\input [6]), .ALU_output(ALU_output));

  // Other names for the same wires on the sheet: is_R_inst = \input [0]; funct[5:0] = in_1[5:0];
  //   instruction[31:0] = in_1; OP[5:0] = in_1[31:26]
endmodule

module rw (
  input  is_funct,
  input  funct6,
  input  funct5,
  input  funct4,
  input  funct3,
  input  funct2,
  input  funct1,
  output rw_0,
  output rw_1
);

  wire and_1_out, and_2_out, and_3_out, and_4_out, and_5_out, and_6_out, not_2_out, not_3_out, not_4_out,
       not_5_out, not_6_out, not_7_out, not_8_out, not_9_out;

  not not_1 (rw_0, is_funct);
  not not_2 (not_2_out, is_funct);
  not not_3 (not_3_out, funct2);
  not not_4 (not_4_out, is_funct);
  not not_5 (not_5_out, funct1);
  not not_6 (not_6_out, is_funct);
  not not_7 (not_7_out, is_funct);
  not not_8 (not_8_out, is_funct);
  not not_9 (not_9_out, is_funct);
  and and_1 (and_1_out, not_2_out, not_3_out);
  and and_2 (and_2_out, not_4_out, not_5_out);
  and and_3 (and_3_out, not_6_out, funct3);
  and and_4 (and_4_out, not_7_out, funct4);
  and and_5 (and_5_out, not_8_out, funct5);
  and and_6 (and_6_out, not_9_out, funct6);
  or or_1 (rw_1, and_1_out, and_2_out, and_3_out, and_4_out, and_5_out, and_6_out);
endmodule

module Ra (
  input  is_funct,
  input  funct6,
  input  funct5,
  input  funct4,
  input  funct3,
  input  funct2,
  input  funct1,
  output Ra_0,
  output Ra_1
);

  wire and_1_out, and_2_out, and_3_out, and_4_out, and_5_out, not_1_out, not_2_out, not_3_out, not_4_out,
       not_5_out, not_6_out, not_7_out, not_8_out, not_9_out, not_10_out, not_11_out, not_12_out, not_13_out,
       not_14_out, not_15_out, not_16_out, not_17_out, not_18_out, not_19_out, not_20_out;

  not not_1 (not_1_out, funct6);
  not not_2 (not_2_out, funct5);
  not not_3 (not_3_out, funct4);
  not not_4 (not_4_out, funct3);
  not not_5 (not_5_out, funct1);
  not not_6 (not_6_out, funct6);
  not not_7 (not_7_out, funct5);
  not not_8 (not_8_out, funct4);
  not not_9 (not_9_out, funct6);
  not not_10 (not_10_out, funct5);
  not not_11 (not_11_out, funct2);
  not not_12 (not_12_out, funct1);
  not not_13 (not_13_out, funct6);
  not not_14 (not_14_out, funct5);
  not not_15 (not_15_out, funct4);
  not not_16 (not_16_out, funct3);
  not not_17 (not_17_out, funct1);
  not not_18 (not_18_out, funct6);
  not not_19 (not_19_out, funct5);
  not not_20 (not_20_out, funct4);
  and and_1 (and_1_out, is_funct, not_1_out, not_2_out, not_3_out, not_4_out, not_5_out);
  and and_2 (and_2_out, is_funct, not_6_out, not_7_out, not_8_out, funct2);
  and and_3 (and_3_out, is_funct, not_9_out, not_10_out, funct4, funct3, not_11_out, not_12_out);
  and and_4 (and_4_out, is_funct, not_13_out, not_14_out, not_15_out, not_16_out, not_17_out);
  and and_5 (and_5_out, is_funct, not_18_out, not_19_out, not_20_out, funct2);
  or or_1 (Ra_0, and_1_out, and_2_out, and_3_out);
  or or_2 (Ra_1, and_4_out, and_5_out);
endmodule

module WE (
  input  is_funct,
  input  funct6,
  input  funct5,
  input  funct4,
  input  funct3,
  input  funct2,
  input  funct1,
  output WE
);

  wire and_1_out, and_2_out, and_3_out, and_4_out, and_5_out, and_6_out, and_7_out, and_8_out, and_9_out,
       not_1_out, not_2_out, not_3_out, not_4_out, not_5_out, not_6_out, not_7_out, not_8_out, not_9_out,
       not_10_out, not_11_out, not_12_out, not_13_out, not_14_out, not_15_out, not_16_out, not_17_out,
       not_18_out, not_19_out, not_20_out, not_21_out, not_22_out, not_23_out, not_24_out, not_25_out,
       not_26_out, not_27_out, not_28_out, not_29_out, not_30_out, not_31_out;

  not not_1 (not_1_out, funct6);
  not not_2 (not_2_out, funct5);
  not not_3 (not_3_out, funct4);
  not not_4 (not_4_out, funct3);
  not not_5 (not_5_out, is_funct);
  not not_6 (not_6_out, funct6);
  not not_7 (not_7_out, funct5);
  not not_8 (not_8_out, funct3);
  not not_9 (not_9_out, funct1);
  not not_10 (not_10_out, is_funct);
  not not_11 (not_11_out, funct6);
  not not_12 (not_12_out, funct5);
  not not_13 (not_13_out, funct2);
  not not_14 (not_14_out, is_funct);
  not not_15 (not_15_out, funct5);
  not not_16 (not_16_out, funct4);
  not not_17 (not_17_out, funct3);
  not not_18 (not_18_out, funct5);
  not not_19 (not_19_out, funct4);
  not not_20 (not_20_out, funct3);
  not not_21 (not_21_out, funct1);
  not not_22 (not_22_out, funct6);
  not not_23 (not_23_out, funct5);
  not not_24 (not_24_out, funct4);
  not not_25 (not_25_out, funct5);
  not not_26 (not_26_out, funct4);
  not not_27 (not_27_out, funct2);
  not not_28 (not_28_out, funct5);
  not not_29 (not_29_out, funct4);
  not not_30 (not_30_out, funct5);
  not not_31 (not_31_out, funct3);
  and and_1 (and_1_out, not_1_out, not_2_out, not_3_out, not_4_out, funct2, funct1);
  and and_2 (and_2_out, not_5_out, not_6_out, not_7_out, funct4, not_8_out, not_9_out);
  and and_3 (and_3_out, not_10_out, not_11_out, not_12_out, funct4, not_13_out);
  and and_4 (and_4_out, not_14_out, funct6, not_15_out, not_16_out, not_17_out, funct1);
  and and_5 (and_5_out, is_funct, not_18_out, not_19_out, not_20_out, not_21_out);
  and and_6 (and_6_out, is_funct, not_22_out, not_23_out, not_24_out, funct2);
  and and_7 (and_7_out, is_funct, funct6, not_25_out, not_26_out, not_27_out);
  and and_8 (and_8_out, is_funct, funct6, not_28_out, not_29_out, funct3, funct1);
  and and_9 (and_9_out, is_funct, funct6, not_30_out, funct4, not_31_out, funct2);
  or or_1 (WE, and_1_out, and_2_out, and_3_out, and_4_out, and_5_out, and_6_out, and_7_out, and_8_out, and_9_out);
endmodule

module w (
  input  is_funct,
  input  funct6,
  input  funct5,
  input  funct4,
  input  funct3,
  input  funct2,
  input  funct1,
  output w_0,
  output w_1
);

  wire and_1_out, and_2_out, not_1_out, not_2_out, not_3_out, not_4_out, not_5_out, not_6_out, not_7_out,
       not_8_out, not_9_out, not_10_out, not_11_out, not_12_out;

  not not_1 (not_1_out, is_funct);
  not not_2 (not_2_out, funct5);
  not not_3 (not_3_out, funct4);
  not not_4 (not_4_out, funct3);
  not not_5 (not_5_out, is_funct);
  not not_6 (not_6_out, funct5);
  not not_7 (not_7_out, funct4);
  not not_8 (not_8_out, funct3);
  not not_9 (not_9_out, is_funct);
  not not_10 (not_10_out, funct5);
  not not_11 (not_11_out, funct4);
  not not_12 (not_12_out, funct3);
  and and_1 (and_1_out, not_1_out, not_2_out, not_3_out, not_4_out, funct2, funct1);
  and and_2 (and_2_out, not_5_out, funct6, not_6_out, not_7_out, not_8_out, funct1);
  and and_3 (w_1, not_9_out, funct6, not_10_out, not_11_out, not_12_out, funct1);
  or or_1 (w_0, and_1_out, and_2_out);
endmodule

module Y (
  input  is_funct,
  input  funct6,
  input  funct5,
  input  funct4,
  input  funct3,
  input  funct2,
  input  funct1,
  output Y_0,
  output Y_1
);

  wire and_1_out, and_2_out, and_3_out, and_4_out, and_5_out, and_6_out, and_7_out, and_8_out, and_9_out,
       and_10_out, and_11_out, and_12_out, not_1_out, not_2_out, not_3_out, not_4_out, not_5_out, not_6_out,
       not_7_out, not_8_out, not_9_out, not_10_out, not_11_out, not_12_out, not_13_out, not_14_out,
       not_15_out, not_16_out, not_17_out, not_18_out, not_19_out, not_20_out, not_21_out;

  not not_1 (not_1_out, is_funct);
  not not_2 (not_2_out, funct3);
  not not_3 (not_3_out, funct6);
  not not_4 (not_4_out, funct5);
  not not_5 (not_5_out, funct4);
  not not_6 (not_6_out, funct3);
  not not_7 (not_7_out, funct1);
  not not_8 (not_8_out, funct6);
  not not_9 (not_9_out, funct5);
  not not_10 (not_10_out, funct4);
  not not_11 (not_11_out, funct3);
  not not_12 (not_12_out, is_funct);
  not not_13 (not_13_out, is_funct);
  not not_14 (not_14_out, is_funct);
  not not_15 (not_15_out, is_funct);
  not not_16 (not_16_out, is_funct);
  not not_17 (not_17_out, funct3);
  not not_18 (not_18_out, is_funct);
  not not_19 (not_19_out, is_funct);
  not not_20 (not_20_out, is_funct);
  not not_21 (not_21_out, is_funct);
  and and_1 (and_1_out, not_1_out, not_2_out);
  and and_2 (and_2_out, not_3_out, not_4_out, not_5_out, not_6_out, not_7_out);
  and and_3 (and_3_out, not_8_out, not_9_out, not_10_out, not_11_out, funct2);
  and and_4 (and_4_out, not_12_out, funct2, funct1);
  and and_5 (and_5_out, not_13_out, funct4);
  and and_6 (and_6_out, not_14_out, funct5);
  and and_7 (and_7_out, not_15_out, funct6);
  and and_8 (and_8_out, not_16_out, not_17_out);
  and and_9 (and_9_out, not_18_out, funct2, funct1);
  and and_10 (and_10_out, not_19_out, funct4);
  and and_11 (and_11_out, not_20_out, funct5);
  and and_12 (and_12_out, not_21_out, funct6);
  or or_1 (Y_0, and_1_out, and_2_out, and_3_out, and_4_out, and_5_out, and_6_out, and_7_out);
  or or_2 (Y_1, and_8_out, and_9_out, and_10_out, and_11_out, and_12_out);
endmodule

module ALU_S (
  input  is_funct,
  input  funct6,
  input  funct5,
  input  funct4,
  input  funct3,
  input  funct2,
  input  funct1,
  output ALU_S_4,
  output ALI_S_3,
  output ALI_S_2,
  output ALI_S_1
);

  wire and_1_out, and_2_out, and_3_out, and_4_out, and_5_out, and_6_out, and_7_out, and_8_out, and_9_out,
       and_10_out, and_11_out, and_12_out, and_13_out, and_14_out, and_15_out, and_16_out, and_17_out,
       and_18_out, and_19_out, and_20_out, and_21_out, not_1_out, not_2_out, not_3_out, not_4_out, not_5_out,
       not_6_out, not_7_out, not_8_out, not_9_out, not_10_out, not_11_out, not_12_out, not_13_out,
       not_14_out, not_15_out, not_16_out, not_17_out, not_18_out, not_19_out, not_20_out, not_21_out,
       not_22_out, not_23_out, not_24_out, not_25_out, not_26_out, not_27_out, not_28_out, not_29_out,
       not_30_out, not_31_out, not_32_out;

  not not_1 (not_1_out, is_funct);
  not not_2 (not_2_out, funct1);
  not not_3 (not_3_out, funct2);
  not not_4 (not_4_out, is_funct);
  not not_5 (not_5_out, funct3);
  not not_6 (not_6_out, funct2);
  not not_7 (not_7_out, funct2);
  not not_8 (not_8_out, funct1);
  not not_9 (not_9_out, is_funct);
  not not_10 (not_10_out, funct4);
  not not_11 (not_11_out, funct3);
  not not_12 (not_12_out, is_funct);
  not not_13 (not_13_out, funct1);
  not not_14 (not_14_out, funct5);
  not not_15 (not_15_out, funct4);
  not not_16 (not_16_out, funct1);
  not not_17 (not_17_out, funct1);
  not not_18 (not_18_out, funct5);
  not not_19 (not_19_out, funct4);
  not not_20 (not_20_out, funct3);
  not not_21 (not_21_out, is_funct);
  not not_22 (not_22_out, funct4);
  not not_23 (not_23_out, is_funct);
  not not_24 (not_24_out, funct1);
  not not_25 (not_25_out, funct6);
  not not_26 (not_26_out, funct4);
  not not_27 (not_27_out, funct3);
  not not_28 (not_28_out, funct3);
  not not_29 (not_29_out, funct4);
  not not_30 (not_30_out, funct6);
  not not_31 (not_31_out, funct3);
  not not_32 (not_32_out, funct2);
  and and_1 (and_1_out, not_1_out, funct2, not_2_out);
  and and_2 (and_2_out, funct3, not_3_out, funct1);
  and and_3 (and_3_out, funct6, funct3, funct2);
  and and_4 (and_4_out, is_funct, funct4);
  and and_5 (and_5_out, not_4_out, not_5_out, not_6_out);
  and and_6 (and_6_out, funct3, not_7_out, not_8_out);
  and and_7 (and_7_out, not_9_out, funct6);
  and and_8 (and_8_out, funct6, not_10_out, not_11_out);
  and and_9 (and_9_out, not_12_out, funct2, not_13_out);
  and and_10 (and_10_out, not_14_out, not_15_out, funct2, not_16_out);
  and and_11 (and_11_out, funct3, not_17_out);
  and and_12 (and_12_out, is_funct, funct6, not_18_out, not_19_out, funct2);
  and and_13 (and_13_out, is_funct, funct6, not_20_out, funct2);
  and and_14 (and_14_out, not_21_out, not_22_out);
  and and_15 (and_15_out, not_23_out, not_24_out);
  and and_16 (and_16_out, not_25_out, not_26_out, funct1);
  and and_17 (and_17_out, not_27_out, funct1);
  and and_18 (and_18_out, funct4, not_28_out);
  and and_19 (and_19_out, funct5, not_29_out, funct1);
  and and_20 (and_20_out, not_30_out, funct5, not_31_out, funct2);
  and and_21 (and_21_out, funct6, not_32_out);
  or or_1 (ALU_S_4, and_1_out, and_2_out, and_3_out, and_4_out);
  or or_2 (ALI_S_3, and_5_out, and_6_out, and_7_out, and_8_out);
  or or_3 (ALI_S_2, and_9_out, and_10_out, and_11_out, and_12_out, and_13_out);
  or or_4 (ALI_S_1, and_14_out, and_15_out, and_16_out, and_17_out, and_18_out, and_19_out, and_20_out, and_21_out);
endmodule

module PC_MUX_2 (
  input  is_funct,
  input  funct6,
  input  funct5,
  input  funct4,
  input  funct3,
  input  funct2,
  input  funct1,
  output PC_MUX_2
);

  wire not_1_out;

  not not_1 (not_1_out, funct2);
  or or_1 (PC_MUX_2, not_1_out, funct3, funct4, funct5, funct6, is_funct);
endmodule

module PC_MUX_3 (
  input  is_funct,
  input  funct6,
  input  funct5,
  input  funct4,
  input  funct3,
  input  funct2,
  input  funct1,
  output PC_MUX_3
);

  wire not_1_out, not_2_out, not_3_out, not_4_out, not_5_out;

  not not_1 (not_1_out, funct6);
  not not_2 (not_2_out, funct5);
  not not_3 (not_3_out, funct3);
  not not_4 (not_4_out, funct2);
  not not_5 (not_5_out, funct1);
  and and_1 (PC_MUX_3, is_funct, not_1_out, not_2_out, funct4, not_3_out, not_4_out, not_5_out);
endmodule

module ALU_output (
  input  is_funct,
  input  funct6,
  input  funct5,
  input  funct4,
  input  funct3,
  input  funct2,
  input  funct1,
  output ALU_output
);

  wire and_1_out, and_2_out, and_3_out, not_1_out, not_2_out, not_3_out, not_4_out, not_5_out, not_6_out,
       not_7_out, not_8_out, not_9_out, not_10_out, not_11_out;

  not not_1 (not_1_out, is_funct);
  not not_2 (not_2_out, funct6);
  not not_3 (not_3_out, funct5);
  not not_4 (not_4_out, funct3);
  not not_5 (not_5_out, funct2);
  not not_6 (not_6_out, funct5);
  not not_7 (not_7_out, funct4);
  not not_8 (not_8_out, funct3);
  not not_9 (not_9_out, funct2);
  not not_10 (not_10_out, funct5);
  not not_11 (not_11_out, funct3);
  and and_1 (and_1_out, not_1_out, not_2_out, not_3_out, funct4, not_4_out, not_5_out, funct1);
  and and_2 (and_2_out, is_funct, funct6, not_6_out, not_7_out, not_8_out, not_9_out, funct1);
  and and_3 (and_3_out, is_funct, funct6, not_10_out, funct4, not_11_out, funct2, funct1);
  or or_1 (ALU_output, and_1_out, and_2_out, and_3_out);
endmodule

module summary (
  input  is_funct,
  input  funct6,
  input  funct5,
  input  funct4,
  input  funct3,
  input  funct2,
  input  funct1,
  output blez,
  output beq,
  output bnq,
  output RAM_STO,
  output RAM_LOAD,
  output Half_word,
  output Branch,
  output un_Branch
);

  wire and_7_out, and_8_out, and_9_out, and_10_out, not_1_out, not_2_out, not_3_out, not_4_out, not_5_out,
       not_6_out, not_7_out, not_8_out, not_9_out, not_10_out, not_11_out, not_12_out, not_13_out,
       not_14_out, not_15_out, not_16_out, not_17_out, not_18_out, not_19_out, not_20_out, not_21_out,
       not_22_out, not_23_out, not_24_out, not_25_out, not_26_out, not_27_out, not_28_out, not_29_out,
       not_30_out, not_31_out, not_32_out, not_33_out, not_34_out, not_35_out, not_36_out, not_37_out,
       not_38_out, not_39_out, not_40_out, not_41_out, not_42_out, not_43_out, not_44_out, not_45_out,
       not_46_out, not_47_out, not_48_out;

  not not_1 (not_1_out, is_funct);
  not not_2 (not_2_out, funct6);
  not not_3 (not_3_out, funct5);
  not not_4 (not_4_out, funct4);
  not not_5 (not_5_out, funct1);
  not not_6 (not_6_out, is_funct);
  not not_7 (not_7_out, funct6);
  not not_8 (not_8_out, funct5);
  not not_9 (not_9_out, funct4);
  not not_10 (not_10_out, funct2);
  not not_11 (not_11_out, funct1);
  not not_12 (not_12_out, is_funct);
  not not_13 (not_13_out, funct6);
  not not_14 (not_14_out, funct5);
  not not_15 (not_15_out, funct4);
  not not_16 (not_16_out, funct2);
  not not_17 (not_17_out, is_funct);
  not not_18 (not_18_out, funct5);
  not not_19 (not_19_out, funct3);
  not not_20 (not_20_out, is_funct);
  not not_21 (not_21_out, funct5);
  not not_22 (not_22_out, funct4);
  not not_23 (not_23_out, funct3);
  not not_24 (not_24_out, is_funct);
  not not_25 (not_25_out, funct5);
  not not_26 (not_26_out, funct4);
  not not_27 (not_27_out, funct3);
  not not_28 (not_28_out, funct2);
  not not_29 (not_29_out, is_funct);
  not not_30 (not_30_out, funct6);
  not not_31 (not_31_out, funct5);
  not not_32 (not_32_out, funct4);
  not not_33 (not_33_out, funct2);
  not not_34 (not_34_out, is_funct);
  not not_35 (not_35_out, funct6);
  not not_36 (not_36_out, funct5);
  not not_37 (not_37_out, funct4);
  not not_38 (not_38_out, funct1);
  not not_39 (not_39_out, is_funct);
  not not_40 (not_40_out, funct6);
  not not_41 (not_41_out, funct5);
  not not_42 (not_42_out, funct4);
  not not_43 (not_43_out, funct3);
  not not_44 (not_44_out, funct6);
  not not_45 (not_45_out, funct5);
  not not_46 (not_46_out, funct3);
  not not_47 (not_47_out, funct2);
  not not_48 (not_48_out, funct1);
  and and_1 (blez, not_1_out, not_2_out, not_3_out, not_4_out, funct3, funct2, not_5_out);
  and and_2 (beq, not_6_out, not_7_out, not_8_out, not_9_out, funct3, not_10_out, not_11_out);
  and and_3 (bnq, not_12_out, not_13_out, not_14_out, not_15_out, funct3, not_16_out, funct1);
  and and_4 (RAM_STO, not_17_out, funct6, not_18_out, funct4, not_19_out, funct2, funct1);
  and and_5 (RAM_LOAD, not_20_out, funct6, not_21_out, not_22_out, not_23_out, funct1);
  and and_6 (Half_word, not_24_out, funct6, not_25_out, not_26_out, not_27_out, not_28_out, funct1);
  and and_7 (and_7_out, not_29_out, not_30_out, not_31_out, not_32_out, funct3, not_33_out);
  and and_8 (and_8_out, not_34_out, not_35_out, not_36_out, not_37_out, funct3, not_38_out);
  and and_9 (and_9_out, not_39_out, not_40_out, not_41_out, not_42_out, not_43_out, funct2);
  and and_10 (and_10_out, is_funct, not_44_out, not_45_out, funct4, not_46_out, not_47_out, not_48_out);
  or or_1 (Branch, and_7_out, and_8_out);
  or or_2 (un_Branch, and_9_out, and_10_out);
endmodule

module syscall (
  input  is_funct,
  input  funct6,
  input  funct5,
  input  funct4,
  input  funct3,
  input  funct2,
  input  funct1,
  output syscall
);

  wire not_1_out, not_2_out, not_3_out, not_4_out;

  not not_1 (not_1_out, funct6);
  not not_2 (not_2_out, funct5);
  not not_3 (not_3_out, funct2);
  not not_4 (not_4_out, funct1);
  and and_1 (syscall, is_funct, not_1_out, not_2_out, funct4, funct3, not_3_out, not_4_out);
endmodule
